// Logisim project culmproject.circ as structural Verilog: 25 circuits, main circuit Mainroughwork
module Main (
  input  A1,
  input  A2,
  input  A3,
  input  A4,
  input  A5,
  input  B1,
  input  B2,
  input  B3,
  input  B4,
  input  B5,
  input  Add0Sub1
);

  wire addorsub_1_c1, addorsub_1_c2, addorsub_1_c3, addorsub_1_c4, addorsub_1_c5, addorsub_1_c6,
       baseconverter1_1_q1, baseconverter1_1_q2, baseconverter1_1_q3, baseconverter1_1_q4,
       baseconverter1_1_q5, baseconverter1_1_q6, baseconverter1_1_q7, baseconverter1_2_q1,
       baseconverter1_2_q2, baseconverter1_2_q3, baseconverter1_2_q4, baseconverter1_2_q5,
       baseconverter1_2_q6, baseconverter1_2_q7, baseconverter1_3_q1, baseconverter1_3_q2,
       baseconverter1_3_q3, baseconverter1_3_q4, baseconverter1_3_q5, baseconverter1_3_q6,
       baseconverter1_3_q7, baseconverter2_1_q1, baseconverter2_1_q2, baseconverter2_1_q3,
       baseconverter2_1_q4, baseconverter2_1_q5, baseconverter2_1_q6, baseconverter2_1_q7,
       baseconverter2_2_q1, baseconverter2_2_q2, baseconverter2_2_q3, baseconverter2_2_q4,
       baseconverter2_2_q5, baseconverter2_2_q6, baseconverter2_2_q7, baseconverter2_3_q1,
       baseconverter2_3_q2, baseconverter2_3_q3, baseconverter2_3_q4, baseconverter2_3_q5,
       baseconverter2_3_q6, baseconverter2_3_q7, dflipflop7bit_1_b, dflipflop7bit_1_b1, dflipflop7bit_1_b2,
       dflipflop7bit_1_b3, dflipflop7bit_1_b4, dflipflop7bit_1_b5, dflipflop7bit_1_b6, Equals_out,
       flipper5bit_1_q2, flipper5bit_1_q3, flipper5bit_1_q4, flipper5bit_1_q5, flipper5bit_1_q6,
       flipper5bit_1_sign, flipper5bit_2_q2, flipper5bit_2_q3, flipper5bit_2_q4, flipper5bit_2_q5,
       flipper5bit_2_q6, flipper5bit_2_sign, flipper6bit_1_q1, flipper6bit_1_q2, flipper6bit_1_q3,
       flipper6bit_1_q4, flipper6bit_1_q5, flipper6bit_1_q6, flipper6bit_1_sign, notgate_1_q, orgate_1_q;

  Button Equals (.out(Equals_out));
  flipper5bit flipper5bit_1 (
    .a1(B1), .a2(B2), .a3(B3), .a4(B4), .a5(B5), .sign(flipper5bit_1_sign), .q2(flipper5bit_1_q2),
    .q3(flipper5bit_1_q3), .q4(flipper5bit_1_q4), .q5(flipper5bit_1_q5), .q6(flipper5bit_1_q6));
  flipper5bit flipper5bit_2 (
    .a1(A1), .a2(A2), .a3(A3), .a4(A4), .a5(A5), .sign(flipper5bit_2_sign), .q2(flipper5bit_2_q2),
    .q3(flipper5bit_2_q3), .q4(flipper5bit_2_q4), .q5(flipper5bit_2_q5), .q6(flipper5bit_2_q6));
  BaseConverter1 baseconverter1_1 (
    .B(flipper5bit_1_q2), .C(flipper5bit_1_q3), .D(flipper5bit_1_q4), .E(flipper5bit_1_q5),
    .F(flipper5bit_1_q6), .Q1(baseconverter1_1_q1), .Q2(baseconverter1_1_q2), .Q3(baseconverter1_1_q3),
    .Q4(baseconverter1_1_q4), .Q5(baseconverter1_1_q5), .Q6(baseconverter1_1_q6), .Q7(baseconverter1_1_q7));  // open: A
  BaseConverter2 baseconverter2_1 (
    .B(flipper5bit_1_q2), .C(flipper5bit_1_q3), .D(flipper5bit_1_q4), .E(flipper5bit_1_q5),
    .F(flipper5bit_1_q6), .Q1(baseconverter2_1_q1), .Q2(baseconverter2_1_q2), .Q3(baseconverter2_1_q3),
    .Q4(baseconverter2_1_q4), .Q5(baseconverter2_1_q5), .Q6(baseconverter2_1_q6), .Q7(baseconverter2_1_q7));  // open: A
  Notgate notgate_1 (.a(Add0Sub1), .Q(notgate_1_q));
  BaseConverter1 baseconverter1_2 (
    .B(flipper5bit_2_q2), .C(flipper5bit_2_q3), .D(flipper5bit_2_q4), .E(flipper5bit_2_q5),
    .F(flipper5bit_2_q6), .Q1(baseconverter1_2_q1), .Q2(baseconverter1_2_q2), .Q3(baseconverter1_2_q3),
    .Q4(baseconverter1_2_q4), .Q5(baseconverter1_2_q5), .Q6(baseconverter1_2_q6), .Q7(baseconverter1_2_q7));  // open: A
  BaseConverter2 baseconverter2_2 (
    .B(flipper5bit_2_q2), .C(flipper5bit_2_q3), .D(flipper5bit_2_q4), .E(flipper5bit_2_q5),
    .F(flipper5bit_2_q6), .Q1(baseconverter2_2_q1), .Q2(baseconverter2_2_q2), .Q3(baseconverter2_2_q3),
    .Q4(baseconverter2_2_q4), .Q5(baseconverter2_2_q5), .Q6(baseconverter2_2_q6), .Q7(baseconverter2_2_q7));  // open: A
  addorsub addorsub_1 (
    .a1(A1), .a2(A2), .a3(A3), .a4(A4), .a5(A5), .b1(B1), .b2(B2), .b3(B3), .b4(B4), .b5(B5),
    .Swap(Add0Sub1), .c1(addorsub_1_c1), .c2(addorsub_1_c2), .c3(addorsub_1_c3), .c4(addorsub_1_c4),
    .c5(addorsub_1_c5), .c6(addorsub_1_c6));
  _7_Segment_Display u_7_segment_display_1 (.g(flipper5bit_2_sign));  // open: f, a, b, e, d, c, dp
  _7_Segment_Display u_7_segment_display_2 (
    .g(baseconverter1_2_q1), .f(baseconverter1_2_q2), .a(baseconverter1_2_q3), .b(baseconverter1_2_q4),
    .e(baseconverter1_2_q5), .d(baseconverter1_2_q6), .c(baseconverter1_2_q7));  // open: dp
  _7_Segment_Display u_7_segment_display_3 (
    .g(baseconverter2_2_q1), .f(baseconverter2_2_q2), .a(baseconverter2_2_q3), .b(baseconverter2_2_q4),
    .e(baseconverter2_2_q5), .d(baseconverter2_2_q6), .c(baseconverter2_2_q7));  // open: dp
  Orgate orgate_1 (.a(notgate_1_q), .b(Add0Sub1), .Q(orgate_1_q));
  LED led_1 (.in(notgate_1_q));
  LED led_2 (.in(orgate_1_q));
  LED led_3 (.in(orgate_1_q));
  LED led_4 (.in(orgate_1_q));
  LED led_5 (.in(notgate_1_q));
  flipper6bit flipper6bit_1 (
    .a1(addorsub_1_c1), .a2(addorsub_1_c2), .a3(addorsub_1_c3), .a4(addorsub_1_c4), .a5(addorsub_1_c5),
    .a6(addorsub_1_c6), .sign(flipper6bit_1_sign), .q1(flipper6bit_1_q1), .q2(flipper6bit_1_q2),
    .q3(flipper6bit_1_q3), .q4(flipper6bit_1_q4), .q5(flipper6bit_1_q5), .q6(flipper6bit_1_q6));
  _7_Segment_Display u_7_segment_display_4 (.g(flipper5bit_1_sign));  // open: f, a, b, e, d, c, dp
  _7_Segment_Display u_7_segment_display_5 (
    .g(baseconverter1_1_q1), .f(baseconverter1_1_q2), .a(baseconverter1_1_q3), .b(baseconverter1_1_q4),
    .e(baseconverter1_1_q5), .d(baseconverter1_1_q6), .c(baseconverter1_1_q7));  // open: dp
  _7_Segment_Display u_7_segment_display_6 (
    .g(baseconverter2_1_q1), .f(baseconverter2_1_q2), .a(baseconverter2_1_q3), .b(baseconverter2_1_q4),
    .e(baseconverter2_1_q5), .d(baseconverter2_1_q6), .c(baseconverter2_1_q7));  // open: dp
  Dflipflop7bit dflipflop7bit_1 (
    .a(flipper6bit_1_sign), .a1(flipper6bit_1_q1), .a2(flipper6bit_1_q2), .a3(flipper6bit_1_q3),
    .a4(flipper6bit_1_q4), .a5(flipper6bit_1_q5), .a6(flipper6bit_1_q6), .Clock(Equals_out),
    .b(dflipflop7bit_1_b), .b1(dflipflop7bit_1_b1), .b2(dflipflop7bit_1_b2), .b3(dflipflop7bit_1_b3),
    .b4(dflipflop7bit_1_b4), .b5(dflipflop7bit_1_b5), .b6(dflipflop7bit_1_b6));
  LED led_6 (.in(Equals_out));
  LED led_7 (.in(Equals_out));
  _7_Segment_Display u_7_segment_display_7 (.g(dflipflop7bit_1_b));  // open: f, a, b, e, d, c, dp
  LED led_8 (.in(Equals_out));
  LED led_9 (.in(Equals_out));
  LED led_10 (.in(Equals_out));
  LED led_11 (.in(Equals_out));
  _7_Segment_Display u_7_segment_display_8 (
    .g(baseconverter1_3_q1), .f(baseconverter1_3_q2), .a(baseconverter1_3_q3), .b(baseconverter1_3_q4),
    .e(baseconverter1_3_q5), .d(baseconverter1_3_q6), .c(baseconverter1_3_q7));  // open: dp
  _7_Segment_Display u_7_segment_display_9 (
    .g(baseconverter2_3_q1), .f(baseconverter2_3_q2), .a(baseconverter2_3_q3), .b(baseconverter2_3_q4),
    .e(baseconverter2_3_q5), .d(baseconverter2_3_q6), .c(baseconverter2_3_q7));  // open: dp
  BaseConverter1 baseconverter1_3 (
    .A(dflipflop7bit_1_b1), .B(dflipflop7bit_1_b2), .C(dflipflop7bit_1_b3), .D(dflipflop7bit_1_b4),
    .E(dflipflop7bit_1_b5), .F(dflipflop7bit_1_b6), .Q1(baseconverter1_3_q1), .Q2(baseconverter1_3_q2),
    .Q3(baseconverter1_3_q3), .Q4(baseconverter1_3_q4), .Q5(baseconverter1_3_q5), .Q6(baseconverter1_3_q6),
    .Q7(baseconverter1_3_q7));
  BaseConverter2 baseconverter2_3 (
    .A(dflipflop7bit_1_b1), .B(dflipflop7bit_1_b2), .C(dflipflop7bit_1_b3), .D(dflipflop7bit_1_b4),
    .E(dflipflop7bit_1_b5), .F(dflipflop7bit_1_b6), .Q1(baseconverter2_3_q1), .Q2(baseconverter2_3_q2),
    .Q3(baseconverter2_3_q3), .Q4(baseconverter2_3_q4), .Q5(baseconverter2_3_q5), .Q6(baseconverter2_3_q6),
    .Q7(baseconverter2_3_q7));
endmodule

module Mainroughwork (
  input  B1,
  input  B2,
  input  B3,
  input  B4,
  input  B5,
  input  A1,
  input  A2,
  input  A3,
  input  A4,
  input  A5,
  input  add0sub1,
  input  Equals,
  output out_13,
  output out_14,
  output out_15,
  output out_16,
  output out_17,
  output out_18
);

  wire addorsub_1_c1, addorsub_1_c2, addorsub_1_c3, addorsub_1_c4, addorsub_1_c5, addorsub_1_c6,
       baseconverter1_1_q1, baseconverter1_1_q2, baseconverter1_1_q3, baseconverter1_1_q4,
       baseconverter1_1_q5, baseconverter1_1_q6, baseconverter1_1_q7, baseconverter1_2_q1,
       baseconverter1_2_q2, baseconverter1_2_q3, baseconverter1_2_q4, baseconverter1_2_q5,
       baseconverter1_2_q6, baseconverter1_2_q7, baseconverter1_3_q1, baseconverter1_3_q2,
       baseconverter1_3_q3, baseconverter1_3_q4, baseconverter1_3_q5, baseconverter1_3_q6,
       baseconverter1_3_q7, baseconverter2_1_q1, baseconverter2_1_q2, baseconverter2_1_q3,
       baseconverter2_1_q4, baseconverter2_1_q5, baseconverter2_1_q6, baseconverter2_1_q7,
       baseconverter2_2_q1, baseconverter2_2_q2, baseconverter2_2_q3, baseconverter2_2_q4,
       baseconverter2_2_q5, baseconverter2_2_q6, baseconverter2_2_q7, baseconverter2_3_q1,
       baseconverter2_3_q2, baseconverter2_3_q3, baseconverter2_3_q4, baseconverter2_3_q5,
       baseconverter2_3_q6, baseconverter2_3_q7, dflipflop7bit_1_b, flipper6bit_1_q1, flipper6bit_1_q2,
       flipper6bit_1_q3, flipper6bit_1_q4, flipper6bit_1_q5, flipper6bit_1_q6, flipper6bit_1_sign,
       flipper6bit_2_p3, flipper6bit_2_p5, flipper6bit_2_p6, flipper6bit_2_p7, flipper6bit_2_p8,
       flipper6bit_2_p9, flipper6bit_2_p10, flipper6bit_3_q1, flipper6bit_3_q2, flipper6bit_3_q3,
       flipper6bit_3_q4, flipper6bit_3_q5, flipper6bit_3_q6, flipper6bit_3_sign;

  flipper6bit flipper6bit_1 (
    .a1(B1), .a2(B2), .a3(B3), .a4(B4), .a5(B5), .sign(flipper6bit_1_sign), .q1(flipper6bit_1_q1),
    .q2(flipper6bit_1_q2), .q3(flipper6bit_1_q3), .q4(flipper6bit_1_q4), .q5(flipper6bit_1_q5),
    .q6(flipper6bit_1_q6));  // open: a6
  // flipper6bit flipper6bit_2: pin names not known; wires that end beside it: A3, A2, flipper6bit_2_p3, A1, flipper6bit_2_p5, flipper6bit_2_p6, flipper6bit_2_p7, flipper6bit_2_p8, flipper6bit_2_p9, flipper6bit_2_p10
  BaseConverter1 baseconverter1_1 (
    .A(flipper6bit_2_p9), .B(flipper6bit_2_p8), .C(flipper6bit_2_p7), .D(flipper6bit_2_p6),
    .E(flipper6bit_2_p5), .F(flipper6bit_2_p3), .Q1(baseconverter1_1_q1), .Q2(baseconverter1_1_q2),
    .Q3(baseconverter1_1_q3), .Q4(baseconverter1_1_q4), .Q5(baseconverter1_1_q5), .Q6(baseconverter1_1_q6),
    .Q7(baseconverter1_1_q7));
  addorsub addorsub_1 (
    .a2(B2), .a3(B3), .a4(B4), .a5(B5), .b1(A1), .b2(A2), .b3(A3), .b4(A4), .b5(A5), .Swap(add0sub1),
    .c1(addorsub_1_c1), .c2(addorsub_1_c2), .c3(addorsub_1_c3), .c4(addorsub_1_c4), .c5(addorsub_1_c5),
    .c6(addorsub_1_c6));  // open: a1
  _7_Segment_Display u_7_segment_display_1 (.g(flipper6bit_2_p10));  // open: f, a, b, e, d, c, dp
  _7_Segment_Display u_7_segment_display_2 (
    .g(baseconverter1_1_q1), .f(baseconverter1_1_q2), .a(baseconverter1_1_q3), .b(baseconverter1_1_q4),
    .e(baseconverter1_1_q5), .d(baseconverter1_1_q6), .c(baseconverter1_1_q7));  // open: dp
  BaseConverter2 baseconverter2_1 (
    .A(flipper6bit_2_p9), .B(flipper6bit_2_p8), .C(flipper6bit_2_p7), .D(flipper6bit_2_p6),
    .E(flipper6bit_2_p5), .F(flipper6bit_2_p3), .Q1(baseconverter2_1_q1), .Q2(baseconverter2_1_q2),
    .Q3(baseconverter2_1_q3), .Q4(baseconverter2_1_q4), .Q5(baseconverter2_1_q5), .Q6(baseconverter2_1_q6),
    .Q7(baseconverter2_1_q7));
  _7_Segment_Display u_7_segment_display_3 (
    .g(baseconverter2_1_q1), .f(baseconverter2_1_q2), .a(baseconverter2_1_q3), .b(baseconverter2_1_q4),
    .e(baseconverter2_1_q5), .d(baseconverter2_1_q6), .c(baseconverter2_1_q7));  // open: dp
  _7_Segment_Display u_7_segment_display_4 (.g(flipper6bit_1_sign));  // open: f, a, b, e, d, c, dp
  BaseConverter1 baseconverter1_2 (
    .A(flipper6bit_1_q1), .B(flipper6bit_1_q2), .C(flipper6bit_1_q3), .D(flipper6bit_1_q4),
    .E(flipper6bit_1_q5), .F(flipper6bit_1_q6), .Q1(baseconverter1_2_q1), .Q2(baseconverter1_2_q2),
    .Q3(baseconverter1_2_q3), .Q4(baseconverter1_2_q4), .Q5(baseconverter1_2_q5), .Q6(baseconverter1_2_q6),
    .Q7(baseconverter1_2_q7));
  flipper6bit flipper6bit_3 (
    .a1(addorsub_1_c1), .a2(addorsub_1_c2), .a3(addorsub_1_c3), .a4(addorsub_1_c4), .a5(addorsub_1_c5),
    .a6(addorsub_1_c6), .sign(flipper6bit_3_sign), .q1(flipper6bit_3_q1), .q2(flipper6bit_3_q2),
    .q3(flipper6bit_3_q3), .q4(flipper6bit_3_q4), .q5(flipper6bit_3_q5), .q6(flipper6bit_3_q6));
  _7_Segment_Display u_7_segment_display_5 (
    .g(baseconverter2_2_q1), .f(baseconverter2_2_q2), .a(baseconverter2_2_q3), .b(baseconverter2_2_q4),
    .e(baseconverter2_2_q5), .d(baseconverter2_2_q6), .c(baseconverter2_2_q7));  // open: dp
  _7_Segment_Display u_7_segment_display_6 (
    .g(baseconverter1_2_q1), .f(baseconverter1_2_q2), .a(baseconverter1_2_q3), .b(baseconverter1_2_q4),
    .e(baseconverter1_2_q5), .d(baseconverter1_2_q6), .c(baseconverter1_2_q7));  // open: dp
  BaseConverter2 baseconverter2_2 (
    .A(flipper6bit_1_q1), .B(flipper6bit_1_q2), .C(flipper6bit_1_q3), .D(flipper6bit_1_q4),
    .E(flipper6bit_1_q5), .F(flipper6bit_1_q6), .Q1(baseconverter2_2_q1), .Q2(baseconverter2_2_q2),
    .Q3(baseconverter2_2_q3), .Q4(baseconverter2_2_q4), .Q5(baseconverter2_2_q5), .Q6(baseconverter2_2_q6),
    .Q7(baseconverter2_2_q7));
  _7_Segment_Display u_7_segment_display_7 (.g(dflipflop7bit_1_b));  // open: f, a, b, e, d, c, dp
  _7_Segment_Display u_7_segment_display_8 (
    .g(baseconverter1_3_q1), .f(baseconverter1_3_q2), .a(baseconverter1_3_q3), .b(baseconverter1_3_q4),
    .e(baseconverter1_3_q5), .d(baseconverter1_3_q6), .c(baseconverter1_3_q7));  // open: dp
  Dflipflop7bit dflipflop7bit_1 (
    .a(flipper6bit_3_sign), .a1(flipper6bit_3_q1), .a2(flipper6bit_3_q2), .a3(flipper6bit_3_q3),
    .a4(flipper6bit_3_q4), .a5(flipper6bit_3_q5), .a6(flipper6bit_3_q6), .Clock(Equals),
    .b(dflipflop7bit_1_b), .b1(out_13), .b2(out_14), .b3(out_15), .b4(out_16), .b5(out_17), .b6(out_18));
  _7_Segment_Display u_7_segment_display_9 (
    .g(baseconverter2_3_q1), .f(baseconverter2_3_q2), .a(baseconverter2_3_q3), .b(baseconverter2_3_q4),
    .e(baseconverter2_3_q5), .d(baseconverter2_3_q6), .c(baseconverter2_3_q7));  // open: dp
  _7_Segment_Display u_7_segment_display_10 (.g(dflipflop7bit_1_b));  // open: f, a, b, e, d, c, dp
  _7_Segment_Display u_7_segment_display_11 (
    .g(baseconverter1_3_q1), .f(baseconverter1_3_q2), .a(baseconverter1_3_q3), .b(baseconverter1_3_q4),
    .e(baseconverter1_3_q5), .d(baseconverter1_3_q6), .c(baseconverter1_3_q7));  // open: dp
  _7_Segment_Display u_7_segment_display_12 (
    .g(baseconverter2_3_q1), .f(baseconverter2_3_q2), .a(baseconverter2_3_q3), .b(baseconverter2_3_q4),
    .e(baseconverter2_3_q5), .d(baseconverter2_3_q6), .c(baseconverter2_3_q7));  // open: dp
  BaseConverter2 baseconverter2_3 (
    .A(out_13), .B(out_14), .C(out_15), .D(out_16), .E(out_17), .F(out_18), .Q1(baseconverter2_3_q1),
    .Q2(baseconverter2_3_q2), .Q3(baseconverter2_3_q3), .Q4(baseconverter2_3_q4), .Q5(baseconverter2_3_q5),
    .Q6(baseconverter2_3_q6), .Q7(baseconverter2_3_q7));
  BaseConverter1 baseconverter1_3 (
    .A(out_13), .B(out_14), .C(out_15), .D(out_16), .E(out_17), .F(out_18), .Q1(baseconverter1_3_q1),
    .Q2(baseconverter1_3_q2), .Q3(baseconverter1_3_q3), .Q4(baseconverter1_3_q4), .Q5(baseconverter1_3_q5),
    .Q6(baseconverter1_3_q6), .Q7(baseconverter1_3_q7));
endmodule

module Norgate (
  input  a,
  input  b,
  output Q
);

  wire transistor_2_out;

  Transistor #(.\type ("n")) transistor_1 (.in(1'b0), .out(Q), .gate(a));
  Transistor transistor_2 (.in(1'b1), .out(transistor_2_out), .gate(a));
  Transistor transistor_3 (.in(transistor_2_out), .out(Q), .gate(b));
  Transistor #(.\type ("n")) transistor_4 (.in(1'b0), .out(Q), .gate(b));
endmodule

module Orgate (
  input  a,
  input  b,
  output Q
);

  wire transistor_1_out, transistor_2_out;

  Transistor transistor_1 (.in(1'b1), .out(transistor_1_out), .gate(a));
  Transistor transistor_2 (.in(transistor_1_out), .out(transistor_2_out), .gate(b));
  Transistor #(.\type ("n")) transistor_3 (.in(1'b0), .out(transistor_2_out), .gate(a));
  Transistor #(.\type ("n")) transistor_4 (.in(1'b0), .out(transistor_2_out), .gate(b));
  Transistor transistor_5 (.in(1'b1), .out(Q), .gate(transistor_2_out));
  Transistor #(.\type ("n")) transistor_6 (.in(1'b0), .out(Q), .gate(transistor_2_out));
endmodule

module Andgate (
  input  a,
  input  b,
  output Q
);

  wire transistor_1_out, transistor_3_out;

  Transistor transistor_1 (.in(1'b1), .out(transistor_1_out), .gate(a));
  Transistor #(.\type ("n")) transistor_2 (.in(transistor_3_out), .out(transistor_1_out), .gate(a));
  Transistor #(.\type ("n")) transistor_3 (.in(1'b0), .out(transistor_3_out), .gate(b));
  Transistor transistor_4 (.in(1'b1), .out(transistor_1_out), .gate(b));
  Transistor transistor_5 (.in(1'b1), .out(Q), .gate(transistor_1_out));
  Transistor #(.\type ("n")) transistor_6 (.in(1'b0), .out(Q), .gate(transistor_1_out));
endmodule

module Nandgate (
  input  a,
  input  b,
  output Q
);

  wire transistor_3_out;

  Transistor transistor_1 (.in(1'b1), .out(Q), .gate(a));
  Transistor #(.\type ("n")) transistor_2 (.in(transistor_3_out), .out(Q), .gate(a));
  Transistor #(.\type ("n")) transistor_3 (.in(1'b0), .out(transistor_3_out), .gate(b));
  Transistor transistor_4 (.in(1'b1), .out(Q), .gate(b));
endmodule

module Notgate (
  input  a,
  output Q
);

  Transistor transistor_1 (.in(1'b1), .out(Q), .gate(a));
  Transistor #(.\type ("n")) transistor_2 (.in(1'b0), .out(Q), .gate(a));
endmodule

module Xorgate (
  input  a,
  input  b,
  output Q
);

  wire transistor_1_out, transistor_3_out, transistor_5_out, transistor_7_out, transistor_8_out,
       transistor_11_out, transistor_15_out;

  Transistor transistor_1 (.in(1'b1), .out(transistor_1_out), .gate(a));
  Transistor #(.\type ("n")) transistor_2 (.in(transistor_3_out), .out(transistor_1_out), .gate(a));
  Transistor #(.\type ("n")) transistor_3 (.in(1'b0), .out(transistor_3_out), .gate(b));
  Transistor transistor_4 (.in(1'b1), .out(transistor_1_out), .gate(b));
  Transistor transistor_5 (.in(1'b1), .out(transistor_5_out), .gate(a));
  Transistor #(.\type ("n")) transistor_6 (.in(transistor_7_out), .out(transistor_5_out), .gate(a));
  Transistor #(.\type ("n")) transistor_7 (.in(1'b0), .out(transistor_7_out), .gate(transistor_1_out));
  Transistor transistor_8 (.in(1'b1), .out(transistor_8_out), .gate(transistor_1_out));
  Transistor transistor_9 (.in(1'b1), .out(transistor_8_out), .gate(b));
  Transistor #(.\type ("n")) transistor_10 (.in(transistor_11_out), .out(transistor_8_out), .gate(transistor_1_out));
  Transistor #(.\type ("n")) transistor_11 (.in(1'b0), .out(transistor_11_out), .gate(b));
  Transistor transistor_12 (.in(1'b1), .out(transistor_5_out), .gate(transistor_1_out));
  Transistor transistor_13 (.in(1'b1), .out(Q), .gate(transistor_5_out));
  Transistor #(.\type ("n")) transistor_14 (.in(transistor_15_out), .out(Q), .gate(transistor_5_out));
  Transistor #(.\type ("n")) transistor_15 (.in(1'b0), .out(transistor_15_out), .gate(transistor_8_out));
  Transistor transistor_16 (.in(1'b1), .out(Q), .gate(transistor_8_out));
endmodule

module nandSRlatch (
  input  Set,
  input  Reset,
  output Q
);

  wire nand_2_out;

  nand nand_1 (Q, Set, nand_2_out);
  nand nand_2 (nand_2_out, Q, Reset);
endmodule

module nandDlatch (
  input  Data,
  input  Enable,
  output Q
);

  wire nand_1_out, nand_2_out, not_1_out;

  not not_1 (not_1_out, Data);
  nand nand_1 (nand_1_out, Data, Enable);
  nand nand_2 (nand_2_out, not_1_out, Enable);
  nandSRlatch nandsrlatch_1 (.Set(nand_1_out), .Reset(nand_2_out), .Q(Q));
endmodule

module nandDflipflop (
  input  Data,
  input  Clock,
  output Q
);

  wire nanddlatch_1_q, not_1_out;

  not not_1 (not_1_out, Clock);
  nandDlatch nanddlatch_1 (.Data(Data), .Enable(not_1_out), .Q(nanddlatch_1_q));
  nandDlatch nanddlatch_2 (.Data(nanddlatch_1_q), .Enable(Clock), .Q(Q));
endmodule

module Dflipflop7bit (
  input  a,
  input  a1,
  input  a2,
  input  a3,
  input  a4,
  input  a5,
  input  a6,
  input  Clock,
  output b,
  output b1,
  output b2,
  output b3,
  output b4,
  output b5,
  output b6
);

  nandDflipflop nanddflipflop_1 (.Data(a), .Clock(Clock), .Q(b));
  nandDflipflop nanddflipflop_2 (.Data(a1), .Clock(Clock), .Q(b1));
  nandDflipflop nanddflipflop_3 (.Data(a2), .Clock(Clock), .Q(b2));
  nandDflipflop nanddflipflop_4 (.Data(a3), .Clock(Clock), .Q(b3));
  nandDflipflop nanddflipflop_5 (.Data(a4), .Clock(Clock), .Q(b4));
  nandDflipflop nanddflipflop_6 (.Data(a5), .Clock(Clock), .Q(b5));
  nandDflipflop nanddflipflop_7 (.Data(a6), .Clock(Clock), .Q(b6));
endmodule

module Halfadder (
  input  A,
  input  B,
  output Q,
  output Carry
);

  Andgate andgate_1 (.a(A), .b(B), .Q(Carry));
  Xorgate xorgate_1 (.a(A), .b(B), .Q(Q));
endmodule

module Fulladder (
  input  Carrybit,
  input  A,
  input  B,
  output Q,
  output C
);

  wire andgate_1_q, halfadder_1_carry, halfadder_1_q;

  Halfadder halfadder_1 (.A(A), .B(B), .Q(halfadder_1_q), .Carry(halfadder_1_carry));
  Andgate andgate_1 (.a(halfadder_1_q), .b(Carrybit), .Q(andgate_1_q));
  Xorgate xorgate_1 (.a(halfadder_1_q), .b(Carrybit), .Q(Q));
  Orgate orgate_1 (.a(halfadder_1_carry), .b(andgate_1_q), .Q(C));
endmodule

module Fivebitadder (
  input  Carry0,
  input  B1,
  input  B2,
  input  B3,
  input  B4,
  input  B5,
  input  A1,
  input  A2,
  input  A3,
  input  A4,
  input  A5,
  output Carry,
  output Q1,
  output Q2,
  output Q3,
  output Q4,
  output Q5
);

  wire fulladder_2_c, fulladder_3_c, fulladder_4_c, fulladder_5_c;

  Fulladder fulladder_1 (.Carrybit(fulladder_2_c), .A(B1), .B(A1), .Q(Q1), .C(Carry));
  Fulladder fulladder_2 (.Carrybit(fulladder_3_c), .A(B2), .B(A2), .Q(Q2), .C(fulladder_2_c));
  Fulladder fulladder_3 (.Carrybit(fulladder_4_c), .A(B3), .B(A3), .Q(Q3), .C(fulladder_3_c));
  Fulladder fulladder_4 (.Carrybit(fulladder_5_c), .A(B4), .B(A4), .Q(Q4), .C(fulladder_4_c));
  Fulladder fulladder_5 (.Carrybit(Carry0), .A(B5), .B(A5), .Q(Q5), .C(fulladder_5_c));
endmodule

module Basicadder (
  input  Carry0,
  input  B0,
  input  B1,
  input  B2,
  input  B3,
  input  B4,
  input  B5,
  input  A0,
  input  A1,
  input  A2,
  input  A3,
  input  A4,
  input  A5,
  output Q0,
  output Q1,
  output Q2,
  output Q3,
  output Q4,
  output Q5
);

  wire fulladder_2_c, fulladder_3_c, fulladder_4_c, fulladder_5_c, fulladder_6_c;

  Fulladder fulladder_1 (.Carrybit(fulladder_2_c), .A(B0), .B(A0), .Q(Q0));  // open: C
  Fulladder fulladder_2 (.Carrybit(fulladder_3_c), .A(B1), .B(A1), .Q(Q1), .C(fulladder_2_c));
  Fulladder fulladder_3 (.Carrybit(fulladder_4_c), .A(B2), .B(A2), .Q(Q2), .C(fulladder_3_c));
  Fulladder fulladder_4 (.Carrybit(fulladder_5_c), .A(B3), .B(A3), .Q(Q3), .C(fulladder_4_c));
  Fulladder fulladder_5 (.Carrybit(fulladder_6_c), .A(B4), .B(A4), .Q(Q4), .C(fulladder_5_c));
  Fulladder fulladder_6 (.Carrybit(Carry0), .A(B5), .B(A5), .Q(Q5), .C(fulladder_6_c));
endmodule

module Halfsubtracter (
  input  A,
  input  B,
  output Q,
  output Borrow
);

  wire notgate_1_q;

  Notgate notgate_1 (.a(A), .Q(notgate_1_q));
  Xorgate xorgate_1 (.a(A), .b(B), .Q(Q));
  Andgate andgate_1 (.a(notgate_1_q), .b(B), .Q(Borrow));
endmodule

module Fullsubtracter (
  input  Lend,
  input  A,
  input  B,
  output Q,
  output Borrow
);

  wire halfsubtracter_1_borrow, halfsubtracter_1_q, halfsubtracter_2_borrow;

  Halfsubtracter halfsubtracter_1 (.A(A), .B(B), .Q(halfsubtracter_1_q), .Borrow(halfsubtracter_1_borrow));
  Halfsubtracter halfsubtracter_2 (.A(halfsubtracter_1_q), .B(Lend), .Q(Q), .Borrow(halfsubtracter_2_borrow));
  Orgate orgate_1 (.a(halfsubtracter_1_borrow), .b(halfsubtracter_2_borrow), .Q(Borrow));
endmodule

module Fivebitsubtracter (
  input  Lend0,
  input  B1,
  input  B2,
  input  B3,
  input  B4,
  input  B5,
  input  A1,
  input  A2,
  input  A3,
  input  A4,
  input  A5,
  output Borrow,
  output Q1,
  output Q2,
  output Q3,
  output Q4,
  output Q5
);

  wire fullsubtracter_2_borrow, fullsubtracter_3_borrow, fullsubtracter_4_borrow, fullsubtracter_5_borrow;

  Fullsubtracter fullsubtracter_1 (.Lend(fullsubtracter_2_borrow), .A(B1), .B(A1), .Q(Q1), .Borrow(Borrow));
  Fullsubtracter fullsubtracter_2 (
    .Lend(fullsubtracter_3_borrow), .A(B2), .B(A2), .Q(Q2), .Borrow(fullsubtracter_2_borrow));
  Fullsubtracter fullsubtracter_3 (
    .Lend(fullsubtracter_4_borrow), .A(B3), .B(A3), .Q(Q3), .Borrow(fullsubtracter_3_borrow));
  Fullsubtracter fullsubtracter_4 (
    .Lend(fullsubtracter_5_borrow), .A(B4), .B(A4), .Q(Q4), .Borrow(fullsubtracter_4_borrow));
  Fullsubtracter fullsubtracter_5 (.Lend(Lend0), .A(B5), .B(A5), .Q(Q5), .Borrow(fullsubtracter_5_borrow));
endmodule

module addorsub (
  input  a1,
  input  a2,
  input  a3,
  input  a4,
  input  a5,
  input  b1,
  input  b2,
  input  b3,
  input  b4,
  input  b5,
  input  Swap,
  output c1,
  output c2,
  output c3,
  output c4,
  output c5,
  output c6
);

  wire fulladder_2_c, fulladder_3_c, fulladder_4_c, fulladder_5_c, fulladder_6_c, multiplexer_1_out,
       multiplexer_2_out, multiplexer_3_out, multiplexer_4_out, multiplexer_5_out, notgate_1_q, notgate_2_q,
       notgate_3_q, notgate_4_q, notgate_5_q;

  Fulladder fulladder_1 (.Carrybit(fulladder_2_c), .A(a1), .B(multiplexer_1_out), .Q(c1));  // open: C
  Notgate notgate_1 (.a(b1), .Q(notgate_1_q));
  Multiplexer multiplexer_1 (.in0(b1), .in1(notgate_1_q), .out(multiplexer_1_out), .sel(Swap));
  Fulladder fulladder_2 (.Carrybit(fulladder_3_c), .A(a1), .B(multiplexer_1_out), .Q(c2), .C(fulladder_2_c));
  Notgate notgate_2 (.a(b2), .Q(notgate_2_q));
  Multiplexer multiplexer_2 (.in0(b2), .in1(notgate_2_q), .out(multiplexer_2_out), .sel(Swap));
  Fulladder fulladder_3 (.Carrybit(fulladder_4_c), .A(a2), .B(multiplexer_2_out), .Q(c3), .C(fulladder_3_c));
  Notgate notgate_3 (.a(b3), .Q(notgate_3_q));
  Multiplexer multiplexer_3 (.in0(b3), .in1(notgate_3_q), .out(multiplexer_3_out), .sel(Swap));
  Fulladder fulladder_4 (.Carrybit(fulladder_5_c), .A(a3), .B(multiplexer_3_out), .Q(c4), .C(fulladder_4_c));
  Notgate notgate_4 (.a(b4), .Q(notgate_4_q));
  Multiplexer multiplexer_4 (.in0(b4), .in1(notgate_4_q), .out(multiplexer_4_out), .sel(Swap));
  Fulladder fulladder_5 (.Carrybit(fulladder_6_c), .A(a4), .B(multiplexer_4_out), .Q(c5), .C(fulladder_5_c));
  Notgate notgate_5 (.a(b5), .Q(notgate_5_q));
  Multiplexer multiplexer_5 (.in0(b5), .in1(notgate_5_q), .out(multiplexer_5_out), .sel(Swap));
  Fulladder fulladder_6 (.Carrybit(Swap), .A(a5), .B(multiplexer_5_out), .Q(c6), .C(fulladder_6_c));
endmodule

module flipper6bit (
  input  a1,
  input  a2,
  input  a3,
  input  a4,
  input  a5,
  input  a6,
  output sign,
  output q1,
  output q2,
  output q3,
  output q4,
  output q5,
  output q6
);

  wire basicadder_1_q0, basicadder_1_q1, basicadder_1_q2, basicadder_1_q3, basicadder_1_q4, basicadder_1_q5,
       notgate_1_q, notgate_2_q, notgate_3_q, notgate_4_q, notgate_5_q, notgate_6_q;

  Notgate notgate_1 (.a(a6), .Q(notgate_1_q));
  Notgate notgate_2 (.a(a5), .Q(notgate_2_q));
  Notgate notgate_3 (.a(a4), .Q(notgate_3_q));
  Notgate notgate_4 (.a(a3), .Q(notgate_4_q));
  Notgate notgate_5 (.a(a2), .Q(notgate_5_q));
  Basicadder basicadder_1 (
    .B1(notgate_5_q), .B2(notgate_4_q), .B3(notgate_3_q), .B4(notgate_2_q), .B5(notgate_1_q), .A5(1'b1),
    .Q0(basicadder_1_q0), .Q1(basicadder_1_q1), .Q2(basicadder_1_q2), .Q3(basicadder_1_q3),
    .Q4(basicadder_1_q4), .Q5(basicadder_1_q5));  // open: Carry0, B0, A0, A1, A2, A3, A4
  Notgate notgate_6 (.a(a1), .Q(notgate_6_q));
  Multiplexer multiplexer_1 (.in0(basicadder_1_q0), .in1(a1), .out(q1), .sel(notgate_6_q));
  Multiplexer multiplexer_2 (.in0(basicadder_1_q1), .in1(a2), .out(q2), .sel(notgate_6_q));
  Multiplexer multiplexer_3 (.in0(basicadder_1_q2), .in1(a3), .out(q3), .sel(notgate_6_q));
  Multiplexer multiplexer_4 (.in0(basicadder_1_q3), .in1(a4), .out(q4), .sel(notgate_6_q));
  Multiplexer multiplexer_5 (.in0(basicadder_1_q4), .in1(a5), .out(q5), .sel(notgate_6_q));
  Multiplexer multiplexer_6 (.in0(basicadder_1_q5), .in1(a6), .out(q6), .sel(notgate_6_q));

  assign sign = a1;
endmodule

module flipper5bit (
  input  a1,
  input  a2,
  input  a3,
  input  a4,
  input  a5,
  output sign,
  output q2,
  output q3,
  output q4,
  output q5,
  output q6
);

  wire basicadder_1_q1, basicadder_1_q2, basicadder_1_q3, basicadder_1_q4, basicadder_1_q5, notgate_1_q,
       notgate_2_q, notgate_3_q, notgate_4_q, notgate_5_q;

  Notgate notgate_1 (.a(a5), .Q(notgate_1_q));
  Notgate notgate_2 (.a(a4), .Q(notgate_2_q));
  Notgate notgate_3 (.a(a3), .Q(notgate_3_q));
  Notgate notgate_4 (.a(a2), .Q(notgate_4_q));
  Basicadder basicadder_1 (
    .B2(notgate_4_q), .B3(notgate_3_q), .B4(notgate_2_q), .B5(notgate_1_q), .A5(1'b1), .Q1(basicadder_1_q1),
    .Q2(basicadder_1_q2), .Q3(basicadder_1_q3), .Q4(basicadder_1_q4), .Q5(basicadder_1_q5));  // open: Carry0, B0, B1, A0, A1, A2, A3, A4, Q0
  Notgate notgate_5 (.a(a1), .Q(notgate_5_q));
  Multiplexer multiplexer_1 (.in0(basicadder_1_q1), .in1(a1), .out(q2), .sel(notgate_5_q));
  Multiplexer multiplexer_2 (.in0(basicadder_1_q2), .in1(a2), .out(q3), .sel(notgate_5_q));
  Multiplexer multiplexer_3 (.in0(basicadder_1_q3), .in1(a3), .out(q4), .sel(notgate_5_q));
  Multiplexer multiplexer_4 (.in0(basicadder_1_q4), .in1(a4), .out(q5), .sel(notgate_5_q));
  Multiplexer multiplexer_5 (.in0(basicadder_1_q5), .in1(a5), .out(q6), .sel(notgate_5_q));

  assign sign = a1;
endmodule

module BaseConverter1work (
  input  A,
  input  B,
  input  C,
  input  D,
  input  E,
  input  F,
  output Q1,
  output Q2,
  output Q3,
  output Q4,
  output Q5,
  output Q6,
  output Q7
);

  wire andgate_1_q, andgate_2_q, andgate_3_q, andgate_4_q, andgate_5_q, andgate_6_q, andgate_7_q,
       andgate_8_q, andgate_9_q, andgate_10_q, andgate_11_q, andgate_12_q, andgate_13_q, andgate_14_q,
       andgate_15_q, andgate_16_q, andgate_17_q, andgate_18_q, andgate_19_q, andgate_20_q, andgate_21_q,
       andgate_22_q, andgate_23_q, andgate_24_q, andgate_25_q, andgate_26_q, andgate_27_q, andgate_28_q,
       andgate_29_q, andgate_30_q, andgate_31_q, andgate_32_q, andgate_33_q, andgate_34_q, andgate_35_q,
       andgate_36_q, andgate_37_q, andgate_38_q, andgate_39_q, andgate_40_q, andgate_41_q, andgate_42_q,
       andgate_43_q, andgate_44_q, andgate_45_q, andgate_46_q, andgate_47_q, andgate_48_q, andgate_49_q,
       andgate_50_q, andgate_51_q, andgate_52_q, andgate_53_q, andgate_54_q, andgate_55_q, andgate_56_q,
       andgate_57_q, andgate_58_q, andgate_59_q, andgate_60_q, notgate_2_q, notgate_8_q, notgate_9_q,
       notgate_10_q, notgate_11_q, notgate_12_q, notgate_14_q, notgate_15_q, notgate_16_q, notgate_17_q,
       notgate_18_q, notgate_20_q, notgate_21_q, notgate_22_q, notgate_23_q, notgate_24_q, notgate_26_q,
       notgate_27_q, notgate_28_q, notgate_29_q, notgate_30_q, notgate_32_q, notgate_33_q, notgate_34_q,
       notgate_35_q, orgate_1_q, orgate_2_q, orgate_4_q, orgate_5_q, orgate_6_q, orgate_7_q, orgate_8_q,
       orgate_9_q, orgate_10_q, orgate_11_q, orgate_12_q, orgate_13_q, orgate_14_q, orgate_15_q, orgate_17_q,
       orgate_18_q, orgate_19_q, orgate_20_q;

  Notgate notgate_1 (.a(A));  // open: Q
  Notgate notgate_2 (.a(B), .Q(notgate_2_q));
  Notgate notgate_3 (.a(C));  // open: Q
  Notgate notgate_4 (.a(D));  // open: Q
  Notgate notgate_5 (.a(E));  // open: Q
  Notgate notgate_6 (.a(F));  // open: Q
  Notgate notgate_7 (.a(A));  // open: Q
  Notgate notgate_8 (.a(B), .Q(notgate_8_q));
  Notgate notgate_9 (.a(C), .Q(notgate_9_q));
  Notgate notgate_10 (.a(D), .Q(notgate_10_q));
  Notgate notgate_11 (.a(E), .Q(notgate_11_q));
  Notgate notgate_12 (.a(F), .Q(notgate_12_q));
  Notgate notgate_13 (.a(A));  // open: Q
  Notgate notgate_14 (.a(B), .Q(notgate_14_q));
  Notgate notgate_15 (.a(C), .Q(notgate_15_q));
  Notgate notgate_16 (.a(D), .Q(notgate_16_q));
  Notgate notgate_17 (.a(E), .Q(notgate_17_q));
  Notgate notgate_18 (.a(F), .Q(notgate_18_q));
  Notgate notgate_19 (.a(A));  // open: Q
  Notgate notgate_20 (.a(B), .Q(notgate_20_q));
  Notgate notgate_21 (.a(C), .Q(notgate_21_q));
  Notgate notgate_22 (.a(D), .Q(notgate_22_q));
  Notgate notgate_23 (.a(E), .Q(notgate_23_q));
  Notgate notgate_24 (.a(F), .Q(notgate_24_q));
  Notgate notgate_25 (.a(A));  // open: Q
  Notgate notgate_26 (.a(B), .Q(notgate_26_q));
  Notgate notgate_27 (.a(C), .Q(notgate_27_q));
  Notgate notgate_28 (.a(D), .Q(notgate_28_q));
  Notgate notgate_29 (.a(E), .Q(notgate_29_q));
  Notgate notgate_30 (.a(F), .Q(notgate_30_q));
  Notgate notgate_31 (.a(A));  // open: Q
  Notgate notgate_32 (.a(B), .Q(notgate_32_q));
  Notgate notgate_33 (.a(C), .Q(notgate_33_q));
  Notgate notgate_34 (.a(D), .Q(notgate_34_q));
  Notgate notgate_35 (.a(E), .Q(notgate_35_q));
  Notgate notgate_36 (.a(F));  // open: Q
  Andgate andgate_1 (.a(notgate_2_q), .b(C), .Q(andgate_1_q));
  Andgate andgate_2 (.a(D), .b(E), .Q(andgate_2_q));
  Andgate andgate_3 (.a(B), .b(C), .Q(andgate_3_q));
  Andgate andgate_4 (.a(notgate_8_q), .b(notgate_9_q), .Q(andgate_4_q));
  Andgate andgate_5 (.a(notgate_8_q), .b(notgate_9_q), .Q(andgate_5_q));
  Andgate andgate_6 (.a(notgate_8_q), .b(notgate_9_q), .Q(andgate_6_q));
  Andgate andgate_7 (.a(notgate_12_q), .b(D), .Q(andgate_7_q));
  Andgate andgate_8 (.a(B), .b(notgate_15_q), .Q(andgate_8_q));
  Andgate andgate_9 (.a(notgate_14_q), .b(notgate_15_q), .Q(andgate_9_q));
  Andgate andgate_10 (.a(notgate_14_q), .b(notgate_15_q), .Q(andgate_10_q));
  Andgate andgate_11 (.a(notgate_14_q), .b(notgate_15_q), .Q(andgate_11_q));
  Andgate andgate_12 (.a(notgate_18_q), .b(D), .Q(andgate_12_q));
  Andgate andgate_13 (.a(B), .b(notgate_16_q), .Q(andgate_13_q));
  Andgate andgate_14 (.a(notgate_14_q), .b(C), .Q(andgate_14_q));
  Andgate andgate_15 (.a(D), .b(E), .Q(andgate_15_q));
  Andgate andgate_16 (.a(notgate_21_q), .b(notgate_22_q), .Q(andgate_16_q));
  Andgate andgate_17 (.a(notgate_20_q), .b(notgate_21_q), .Q(andgate_17_q));
  Andgate andgate_18 (.a(notgate_20_q), .b(C), .Q(andgate_18_q));
  Andgate andgate_19 (.a(D), .b(E), .Q(andgate_19_q));
  Andgate andgate_20 (.a(notgate_20_q), .b(D), .Q(andgate_20_q));
  Andgate andgate_21 (.a(E), .b(notgate_24_q), .Q(andgate_21_q));
  Andgate andgate_22 (.a(notgate_21_q), .b(D), .Q(andgate_22_q));
  Andgate andgate_23 (.a(notgate_23_q), .b(notgate_24_q), .Q(andgate_23_q));
  Andgate andgate_24 (.a(notgate_27_q), .b(notgate_28_q), .Q(andgate_24_q));
  Andgate andgate_25 (.a(notgate_26_q), .b(notgate_27_q), .Q(andgate_25_q));
  Andgate andgate_26 (.a(notgate_26_q), .b(C), .Q(andgate_26_q));
  Andgate andgate_27 (.a(D), .b(E), .Q(andgate_27_q));
  Andgate andgate_28 (.a(notgate_26_q), .b(D), .Q(andgate_28_q));
  Andgate andgate_29 (.a(E), .b(notgate_30_q), .Q(andgate_29_q));
  Andgate andgate_30 (.a(notgate_27_q), .b(D), .Q(andgate_30_q));
  Andgate andgate_31 (.a(notgate_29_q), .b(notgate_30_q), .Q(andgate_31_q));
  Andgate andgate_32 (.a(B), .b(notgate_27_q), .Q(andgate_32_q));
  Andgate andgate_33 (.a(B), .b(notgate_28_q), .Q(andgate_33_q));
  Andgate andgate_34 (.a(notgate_32_q), .b(notgate_33_q), .Q(andgate_34_q));
  Andgate andgate_35 (.a(C), .b(B), .Q(andgate_35_q));
  Andgate andgate_36 (.a(D), .b(notgate_35_q), .Q(andgate_36_q));
  Andgate andgate_37 (.a(B), .b(D), .Q(andgate_37_q));
  Andgate andgate_38 (.a(C), .b(notgate_32_q), .Q(andgate_38_q));
  Andgate andgate_39 (.a(notgate_32_q), .b(C), .Q(andgate_39_q));
  Andgate andgate_40 (.a(andgate_1_q), .b(andgate_2_q), .Q(andgate_40_q));
  Andgate andgate_41 (.a(andgate_3_q), .b(D), .Q(andgate_41_q));
  Andgate andgate_42 (.a(andgate_4_q), .b(notgate_10_q), .Q(andgate_42_q));
  Andgate andgate_43 (.a(andgate_5_q), .b(notgate_11_q), .Q(andgate_43_q));
  Andgate andgate_44 (.a(andgate_6_q), .b(andgate_7_q), .Q(andgate_44_q));
  Andgate andgate_45 (.a(andgate_9_q), .b(notgate_16_q), .Q(andgate_45_q));
  Andgate andgate_46 (.a(andgate_10_q), .b(notgate_17_q), .Q(andgate_46_q));
  Andgate andgate_47 (.a(andgate_11_q), .b(andgate_12_q), .Q(andgate_47_q));
  Andgate andgate_48 (.a(andgate_14_q), .b(andgate_15_q), .Q(andgate_48_q));
  Andgate andgate_49 (.a(andgate_17_q), .b(notgate_23_q), .Q(andgate_49_q));
  Andgate andgate_50 (.a(andgate_18_q), .b(andgate_19_q), .Q(andgate_50_q));
  Andgate andgate_51 (.a(andgate_20_q), .b(andgate_21_q), .Q(andgate_51_q));
  Andgate andgate_52 (.a(andgate_22_q), .b(andgate_23_q), .Q(andgate_52_q));
  Andgate andgate_53 (.a(andgate_25_q), .b(notgate_29_q), .Q(andgate_53_q));
  Andgate andgate_54 (.a(andgate_26_q), .b(andgate_27_q), .Q(andgate_54_q));
  Andgate andgate_55 (.a(andgate_28_q), .b(andgate_29_q), .Q(andgate_55_q));
  Andgate andgate_56 (.a(andgate_30_q), .b(andgate_31_q), .Q(andgate_56_q));
  Orgate orgate_1 (.a(andgate_32_q), .b(andgate_33_q), .Q(orgate_1_q));
  Orgate orgate_2 (.a(andgate_34_q), .b(andgate_35_q), .Q(orgate_2_q));
  Andgate andgate_57 (.a(andgate_36_q), .b(F), .Q(andgate_57_q));
  Andgate andgate_58 (.a(andgate_37_q), .b(E), .Q(andgate_58_q));
  Andgate andgate_59 (.a(andgate_38_q), .b(notgate_35_q), .Q(andgate_59_q));
  Andgate andgate_60 (.a(andgate_39_q), .b(notgate_34_q), .Q(andgate_60_q));
  Orgate orgate_3 (.a(B), .b(andgate_40_q), .Q(Q1));
  Orgate orgate_4 (.a(andgate_41_q), .b(andgate_42_q), .Q(orgate_4_q));
  Orgate orgate_5 (.a(andgate_43_q), .b(andgate_44_q), .Q(orgate_5_q));
  Orgate orgate_6 (.a(andgate_8_q), .b(andgate_45_q), .Q(orgate_6_q));
  Orgate orgate_7 (.a(andgate_46_q), .b(andgate_47_q), .Q(orgate_7_q));
  Orgate orgate_8 (.a(andgate_13_q), .b(andgate_48_q), .Q(orgate_8_q));
  Orgate orgate_9 (.a(andgate_16_q), .b(andgate_49_q), .Q(orgate_9_q));
  Orgate orgate_10 (.a(andgate_51_q), .b(andgate_52_q), .Q(orgate_10_q));
  Orgate orgate_11 (.a(andgate_24_q), .b(andgate_53_q), .Q(orgate_11_q));
  Orgate orgate_12 (.a(andgate_54_q), .b(andgate_55_q), .Q(orgate_12_q));
  Orgate orgate_13 (.a(andgate_56_q), .b(orgate_1_q), .Q(orgate_13_q));
  Orgate orgate_14 (.a(andgate_57_q), .b(andgate_58_q), .Q(orgate_14_q));
  Orgate orgate_15 (.a(andgate_59_q), .b(andgate_60_q), .Q(orgate_15_q));
  Orgate orgate_16 (.a(orgate_4_q), .b(orgate_5_q), .Q(Q2));
  Orgate orgate_17 (.a(orgate_6_q), .b(orgate_7_q), .Q(orgate_17_q));
  Orgate orgate_18 (.a(andgate_50_q), .b(orgate_10_q), .Q(orgate_18_q));
  Orgate orgate_19 (.a(orgate_12_q), .b(orgate_13_q), .Q(orgate_19_q));
  Orgate orgate_20 (.a(orgate_14_q), .b(orgate_15_q), .Q(orgate_20_q));
  Orgate orgate_21 (.a(orgate_17_q), .b(orgate_8_q), .Q(Q3));
  Orgate orgate_22 (.a(orgate_9_q), .b(orgate_18_q), .Q(Q5));
  Orgate orgate_23 (.a(orgate_11_q), .b(orgate_19_q), .Q(Q6));
  Orgate orgate_24 (.a(orgate_2_q), .b(orgate_20_q), .Q(Q7));

  assign Q4 = 1'b1;
endmodule

module BaseConverter1 (
  input  A,
  input  B,
  input  C,
  input  D,
  input  E,
  input  F,
  output Q1,
  output Q2,
  output Q3,
  output Q4,
  output Q5,
  output Q6,
  output Q7
);

  wire baseconverter1work_1_q1, baseconverter1work_1_q2, baseconverter1work_1_q3, baseconverter1work_1_q4,
       baseconverter1work_1_q5, baseconverter1work_1_q6, baseconverter1work_1_q7, notgate_1_q;

  Notgate notgate_1 (.a(A), .Q(notgate_1_q));
  BaseConverter1work baseconverter1work_1 (
    .A(A), .B(B), .C(C), .D(D), .E(E), .F(F), .Q1(baseconverter1work_1_q1), .Q2(baseconverter1work_1_q2),
    .Q3(baseconverter1work_1_q3), .Q4(baseconverter1work_1_q4), .Q5(baseconverter1work_1_q5),
    .Q6(baseconverter1work_1_q6), .Q7(baseconverter1work_1_q7));
  Multiplexer multiplexer_1 (.in0(1'b1), .in1(baseconverter1work_1_q1), .out(Q1), .sel(notgate_1_q));
  Multiplexer multiplexer_2 (.in0(1'b1), .in1(baseconverter1work_1_q2), .out(Q2), .sel(notgate_1_q));
  Multiplexer multiplexer_3 (.in0(1'b0), .in1(baseconverter1work_1_q3), .out(Q3), .sel(notgate_1_q));
  Multiplexer multiplexer_4 (.in0(1'b1), .in1(baseconverter1work_1_q4), .out(Q4), .sel(notgate_1_q));
  Multiplexer multiplexer_5 (.in0(1'b0), .in1(baseconverter1work_1_q5), .out(Q5), .sel(notgate_1_q));
  Multiplexer multiplexer_6 (.in0(1'b0), .in1(baseconverter1work_1_q6), .out(Q6), .sel(notgate_1_q));
  Multiplexer multiplexer_7 (.in0(1'b1), .in1(baseconverter1work_1_q7), .out(Q7), .sel(notgate_1_q));
endmodule

module BaseConverter2 (
  input  A,
  input  B,
  input  C,
  input  D,
  input  E,
  input  F,
  output Q1,
  output Q2,
  output Q3,
  output Q4,
  output Q5,
  output Q6,
  output Q7
);

  wire andgate_1_q, andgate_2_q, andgate_3_q, andgate_4_q, andgate_5_q, andgate_6_q, andgate_7_q,
       andgate_8_q, andgate_9_q, andgate_10_q, andgate_11_q, andgate_12_q, andgate_13_q, andgate_14_q,
       andgate_15_q, andgate_16_q, andgate_17_q, andgate_18_q, andgate_19_q, andgate_20_q, andgate_21_q,
       andgate_22_q, andgate_23_q, andgate_24_q, andgate_25_q, andgate_26_q, andgate_27_q, andgate_28_q,
       andgate_29_q, andgate_30_q, andgate_31_q, andgate_32_q, andgate_33_q, andgate_34_q, andgate_35_q,
       andgate_36_q, andgate_37_q, andgate_38_q, andgate_39_q, andgate_40_q, andgate_41_q, andgate_42_q,
       andgate_43_q, andgate_44_q, andgate_45_q, andgate_46_q, andgate_47_q, andgate_48_q, andgate_49_q,
       andgate_50_q, andgate_51_q, andgate_52_q, andgate_53_q, andgate_54_q, andgate_55_q, andgate_56_q,
       andgate_57_q, andgate_58_q, andgate_59_q, andgate_60_q, andgate_61_q, andgate_62_q, andgate_63_q,
       andgate_64_q, andgate_65_q, andgate_66_q, andgate_67_q, andgate_68_q, andgate_69_q, andgate_70_q,
       andgate_71_q, andgate_72_q, andgate_73_q, andgate_74_q, andgate_75_q, andgate_76_q, andgate_77_q,
       andgate_78_q, andgate_79_q, andgate_80_q, andgate_81_q, andgate_82_q, andgate_83_q, andgate_84_q,
       andgate_85_q, andgate_86_q, andgate_87_q, andgate_88_q, andgate_89_q, andgate_90_q, andgate_91_q,
       andgate_92_q, andgate_93_q, andgate_94_q, andgate_95_q, andgate_96_q, andgate_97_q, andgate_98_q,
       andgate_99_q, andgate_100_q, andgate_101_q, andgate_102_q, andgate_103_q, andgate_104_q,
       andgate_105_q, andgate_106_q, andgate_107_q, andgate_108_q, andgate_109_q, andgate_110_q,
       andgate_111_q, andgate_112_q, andgate_113_q, andgate_114_q, andgate_115_q, andgate_116_q,
       andgate_117_q, andgate_118_q, andgate_119_q, andgate_120_q, andgate_121_q, andgate_122_q,
       andgate_123_q, andgate_124_q, andgate_125_q, andgate_126_q, andgate_127_q, andgate_128_q,
       andgate_129_q, andgate_130_q, andgate_131_q, andgate_132_q, andgate_133_q, andgate_134_q,
       andgate_135_q, andgate_136_q, andgate_137_q, andgate_138_q, andgate_139_q, andgate_140_q,
       andgate_141_q, andgate_142_q, andgate_143_q, andgate_144_q, andgate_145_q, andgate_146_q,
       andgate_147_q, andgate_148_q, andgate_149_q, andgate_150_q, andgate_151_q, andgate_152_q,
       andgate_153_q, andgate_154_q, andgate_155_q, andgate_156_q, andgate_157_q, andgate_158_q,
       andgate_159_q, andgate_160_q, andgate_161_q, andgate_162_q, andgate_163_q, andgate_164_q,
       andgate_165_q, andgate_166_q, andgate_167_q, andgate_168_q, andgate_169_q, andgate_170_q,
       andgate_171_q, andgate_172_q, andgate_173_q, andgate_174_q, andgate_175_q, andgate_176_q,
       andgate_177_q, andgate_178_q, andgate_179_q, andgate_180_q, andgate_181_q, andgate_182_q,
       andgate_183_q, andgate_184_q, andgate_185_q, andgate_186_q, andgate_187_q, andgate_188_q,
       andgate_189_q, andgate_190_q, andgate_191_q, andgate_192_q, andgate_193_q, andgate_194_q,
       andgate_195_q, andgate_196_q, andgate_197_q, andgate_198_q, andgate_199_q, andgate_200_q,
       andgate_201_q, andgate_202_q, andgate_203_q, andgate_204_q, andgate_205_q, andgate_206_q,
       andgate_207_q, andgate_208_q, andgate_209_q, andgate_210_q, andgate_211_q, andgate_212_q,
       andgate_213_q, andgate_214_q, andgate_215_q, andgate_216_q, andgate_217_q, andgate_218_q,
       andgate_219_q, andgate_220_q, andgate_221_q, andgate_222_q, andgate_223_q, andgate_224_q,
       andgate_225_q, andgate_226_q, andgate_227_q, andgate_228_q, andgate_229_q, andgate_230_q,
       andgate_231_q, andgate_232_q, andgate_233_q, andgate_234_q, andgate_235_q, andgate_236_q,
       andgate_237_q, andgate_238_q, andgate_239_q, andgate_240_q, andgate_241_q, andgate_242_q,
       andgate_243_q, andgate_244_q, andgate_245_q, andgate_246_q, andgate_247_q, andgate_248_q,
       andgate_249_q, andgate_250_q, andgate_251_q, andgate_252_q, andgate_253_q, andgate_254_q,
       andgate_255_q, andgate_256_q, andgate_257_q, andgate_258_q, andgate_259_q, andgate_260_q,
       andgate_261_q, andgate_262_q, andgate_263_q, andgate_264_q, andgate_265_q, andgate_266_q,
       andgate_267_q, andgate_268_q, andgate_269_q, andgate_270_q, andgate_271_q, andgate_272_q,
       andgate_273_q, andgate_274_q, andgate_275_q, andgate_276_q, andgate_277_q, andgate_278_q,
       andgate_279_q, andgate_280_q, andgate_281_q, andgate_282_q, andgate_283_q, andgate_284_q,
       andgate_285_q, andgate_286_q, andgate_287_q, andgate_288_q, andgate_289_q, andgate_290_q,
       andgate_291_q, notgate_1_q, notgate_2_q, notgate_3_q, notgate_4_q, notgate_5_q, notgate_6_q,
       notgate_7_q, notgate_8_q, notgate_9_q, notgate_10_q, notgate_11_q, notgate_12_q, notgate_13_q,
       notgate_14_q, notgate_15_q, notgate_16_q, notgate_17_q, notgate_18_q, notgate_19_q, notgate_20_q,
       notgate_21_q, notgate_22_q, notgate_23_q, notgate_24_q, notgate_25_q, notgate_26_q, notgate_27_q,
       notgate_28_q, notgate_29_q, notgate_30_q, notgate_31_q, notgate_32_q, notgate_33_q, notgate_34_q,
       notgate_35_q, notgate_36_q, notgate_37_q, notgate_38_q, notgate_39_q, notgate_40_q, notgate_41_q,
       notgate_42_q, orgate_1_q, orgate_2_q, orgate_3_q, orgate_4_q, orgate_5_q, orgate_6_q, orgate_7_q,
       orgate_8_q, orgate_9_q, orgate_10_q, orgate_11_q, orgate_12_q, orgate_13_q, orgate_14_q, orgate_15_q,
       orgate_16_q, orgate_17_q, orgate_18_q, orgate_19_q, orgate_20_q, orgate_21_q, orgate_22_q,
       orgate_23_q, orgate_24_q, orgate_25_q, orgate_26_q, orgate_27_q, orgate_28_q, orgate_29_q,
       orgate_30_q, orgate_31_q, orgate_32_q, orgate_33_q, orgate_34_q, orgate_35_q, orgate_36_q,
       orgate_37_q, orgate_38_q, orgate_39_q, orgate_40_q, orgate_41_q, orgate_42_q, orgate_43_q,
       orgate_44_q, orgate_45_q, orgate_46_q, orgate_47_q, orgate_48_q, orgate_49_q, orgate_50_q,
       orgate_51_q, orgate_52_q, orgate_53_q, orgate_55_q, orgate_56_q, orgate_57_q, orgate_58_q,
       orgate_59_q, orgate_60_q, orgate_66_q;

  Notgate notgate_1 (.a(A), .Q(notgate_1_q));
  Notgate notgate_2 (.a(B), .Q(notgate_2_q));
  Notgate notgate_3 (.a(C), .Q(notgate_3_q));
  Notgate notgate_4 (.a(D), .Q(notgate_4_q));
  Notgate notgate_5 (.a(E), .Q(notgate_5_q));
  Notgate notgate_6 (.a(F), .Q(notgate_6_q));
  Notgate notgate_7 (.a(A), .Q(notgate_7_q));
  Notgate notgate_8 (.a(B), .Q(notgate_8_q));
  Notgate notgate_9 (.a(C), .Q(notgate_9_q));
  Notgate notgate_10 (.a(D), .Q(notgate_10_q));
  Notgate notgate_11 (.a(E), .Q(notgate_11_q));
  Notgate notgate_12 (.a(F), .Q(notgate_12_q));
  Notgate notgate_13 (.a(A), .Q(notgate_13_q));
  Notgate notgate_14 (.a(B), .Q(notgate_14_q));
  Notgate notgate_15 (.a(C), .Q(notgate_15_q));
  Notgate notgate_16 (.a(D), .Q(notgate_16_q));
  Notgate notgate_17 (.a(E), .Q(notgate_17_q));
  Notgate notgate_18 (.a(F), .Q(notgate_18_q));
  Notgate notgate_19 (.a(A), .Q(notgate_19_q));
  Notgate notgate_20 (.a(B), .Q(notgate_20_q));
  Notgate notgate_21 (.a(C), .Q(notgate_21_q));
  Notgate notgate_22 (.a(D), .Q(notgate_22_q));
  Notgate notgate_23 (.a(E), .Q(notgate_23_q));
  Notgate notgate_24 (.a(F), .Q(notgate_24_q));
  Notgate notgate_25 (.a(A), .Q(notgate_25_q));
  Notgate notgate_26 (.a(B), .Q(notgate_26_q));
  Notgate notgate_27 (.a(C), .Q(notgate_27_q));
  Notgate notgate_28 (.a(D), .Q(notgate_28_q));
  Notgate notgate_29 (.a(E), .Q(notgate_29_q));
  Notgate notgate_30 (.a(F), .Q(notgate_30_q));
  Notgate notgate_31 (.a(A), .Q(notgate_31_q));
  Notgate notgate_32 (.a(B), .Q(notgate_32_q));
  Notgate notgate_33 (.a(C), .Q(notgate_33_q));
  Notgate notgate_34 (.a(D), .Q(notgate_34_q));
  Notgate notgate_35 (.a(E), .Q(notgate_35_q));
  Notgate notgate_36 (.a(F), .Q(notgate_36_q));
  Notgate notgate_37 (.a(A), .Q(notgate_37_q));
  Notgate notgate_38 (.a(B), .Q(notgate_38_q));
  Notgate notgate_39 (.a(C), .Q(notgate_39_q));
  Notgate notgate_40 (.a(D), .Q(notgate_40_q));
  Notgate notgate_41 (.a(E), .Q(notgate_41_q));
  Notgate notgate_42 (.a(F), .Q(notgate_42_q));
  Andgate andgate_1 (.a(notgate_1_q), .b(notgate_2_q), .Q(andgate_1_q));
  Andgate andgate_2 (.a(notgate_3_q), .b(D), .Q(andgate_2_q));
  Andgate andgate_3 (.a(notgate_1_q), .b(notgate_4_q), .Q(andgate_3_q));
  Andgate andgate_4 (.a(notgate_1_q), .b(B), .Q(andgate_4_q));
  Andgate andgate_5 (.a(notgate_1_q), .b(B), .Q(andgate_5_q));
  Andgate andgate_6 (.a(D), .b(F), .Q(andgate_6_q));
  Andgate andgate_7 (.a(notgate_1_q), .b(C), .Q(andgate_7_q));
  Andgate andgate_8 (.a(notgate_4_q), .b(notgate_5_q), .Q(andgate_8_q));
  Andgate andgate_9 (.a(notgate_1_q), .b(B), .Q(andgate_9_q));
  Andgate andgate_10 (.a(C), .b(D), .Q(andgate_10_q));
  Andgate andgate_11 (.a(notgate_1_q), .b(notgate_2_q), .Q(andgate_11_q));
  Andgate andgate_12 (.a(C), .b(D), .Q(andgate_12_q));
  Andgate andgate_13 (.a(notgate_1_q), .b(notgate_3_q), .Q(andgate_13_q));
  Andgate andgate_14 (.a(D), .b(notgate_5_q), .Q(andgate_14_q));
  Andgate andgate_15 (.a(notgate_1_q), .b(C), .Q(andgate_15_q));
  Andgate andgate_16 (.a(D), .b(notgate_5_q), .Q(andgate_16_q));
  Andgate andgate_17 (.a(notgate_1_q), .b(notgate_2_q), .Q(andgate_17_q));
  Andgate andgate_18 (.a(notgate_3_q), .b(D), .Q(andgate_18_q));
  Andgate andgate_19 (.a(A), .b(notgate_2_q), .Q(andgate_19_q));
  Andgate andgate_20 (.a(notgate_3_q), .b(notgate_4_q), .Q(andgate_20_q));
  Andgate andgate_21 (.a(notgate_1_q), .b(notgate_2_q), .Q(andgate_21_q));
  Andgate andgate_22 (.a(C), .b(D), .Q(andgate_22_q));
  Andgate andgate_23 (.a(notgate_7_q), .b(notgate_8_q), .Q(andgate_23_q));
  Andgate andgate_24 (.a(notgate_9_q), .b(D), .Q(andgate_24_q));
  Andgate andgate_25 (.a(notgate_8_q), .b(notgate_7_q), .Q(andgate_25_q));
  Andgate andgate_26 (.a(D), .b(notgate_12_q), .Q(andgate_26_q));
  Andgate andgate_27 (.a(notgate_7_q), .b(notgate_8_q), .Q(andgate_27_q));
  Andgate andgate_28 (.a(D), .b(notgate_11_q), .Q(andgate_28_q));
  Andgate andgate_29 (.a(notgate_7_q), .b(B), .Q(andgate_29_q));
  Andgate andgate_30 (.a(notgate_10_q), .b(E), .Q(andgate_30_q));
  Andgate andgate_31 (.a(notgate_7_q), .b(D), .Q(andgate_31_q));
  Andgate andgate_32 (.a(B), .b(notgate_11_q), .Q(andgate_32_q));
  Andgate andgate_33 (.a(notgate_7_q), .b(B), .Q(andgate_33_q));
  Andgate andgate_34 (.a(C), .b(notgate_11_q), .Q(andgate_34_q));
  Andgate andgate_35 (.a(notgate_8_q), .b(notgate_9_q), .Q(andgate_35_q));
  Andgate andgate_36 (.a(notgate_10_q), .b(notgate_11_q), .Q(andgate_36_q));
  Andgate andgate_37 (.a(notgate_7_q), .b(C), .Q(andgate_37_q));
  Andgate andgate_38 (.a(notgate_10_q), .b(E), .Q(andgate_38_q));
  Andgate andgate_39 (.a(notgate_7_q), .b(B), .Q(andgate_39_q));
  Andgate andgate_40 (.a(notgate_9_q), .b(D), .Q(andgate_40_q));
  Andgate andgate_41 (.a(notgate_13_q), .b(B), .Q(andgate_41_q));
  Andgate andgate_42 (.a(E), .b(F), .Q(andgate_42_q));
  Andgate andgate_43 (.a(notgate_13_q), .b(B), .Q(andgate_43_q));
  Andgate andgate_44 (.a(notgate_15_q), .b(notgate_17_q), .Q(andgate_44_q));
  Andgate andgate_45 (.a(notgate_13_q), .b(C), .Q(andgate_45_q));
  Andgate andgate_46 (.a(D), .b(notgate_18_q), .Q(andgate_46_q));
  Andgate andgate_47 (.a(notgate_13_q), .b(notgate_14_q), .Q(andgate_47_q));
  Andgate andgate_48 (.a(notgate_15_q), .b(E), .Q(andgate_48_q));
  Andgate andgate_49 (.a(notgate_13_q), .b(notgate_14_q), .Q(andgate_49_q));
  Andgate andgate_50 (.a(D), .b(notgate_17_q), .Q(andgate_50_q));
  Andgate andgate_51 (.a(notgate_13_q), .b(notgate_14_q), .Q(andgate_51_q));
  Andgate andgate_52 (.a(C), .b(notgate_17_q), .Q(andgate_52_q));
  Andgate andgate_53 (.a(notgate_13_q), .b(C), .Q(andgate_53_q));
  Andgate andgate_54 (.a(notgate_16_q), .b(E), .Q(andgate_54_q));
  Andgate andgate_55 (.a(notgate_13_q), .b(B), .Q(andgate_55_q));
  Andgate andgate_56 (.a(C), .b(notgate_18_q), .Q(andgate_56_q));
  Andgate andgate_57 (.a(notgate_14_q), .b(notgate_15_q), .Q(andgate_57_q));
  Andgate andgate_58 (.a(notgate_17_q), .b(notgate_18_q), .Q(andgate_58_q));
  Andgate andgate_59 (.a(notgate_19_q), .b(notgate_20_q), .Q(andgate_59_q));
  Andgate andgate_60 (.a(notgate_19_q), .b(E), .Q(andgate_60_q));
  Andgate andgate_61 (.a(D), .b(F), .Q(andgate_61_q));
  Andgate andgate_62 (.a(notgate_19_q), .b(E), .Q(andgate_62_q));
  Andgate andgate_63 (.a(D), .b(C), .Q(andgate_63_q));
  Andgate andgate_64 (.a(notgate_19_q), .b(D), .Q(andgate_64_q));
  Andgate andgate_65 (.a(B), .b(E), .Q(andgate_65_q));
  Andgate andgate_66 (.a(notgate_19_q), .b(B), .Q(andgate_66_q));
  Andgate andgate_67 (.a(C), .b(notgate_23_q), .Q(andgate_67_q));
  Andgate andgate_68 (.a(notgate_19_q), .b(B), .Q(andgate_68_q));
  Andgate andgate_69 (.a(notgate_23_q), .b(F), .Q(andgate_69_q));
  Andgate andgate_70 (.a(notgate_19_q), .b(B), .Q(andgate_70_q));
  Andgate andgate_71 (.a(notgate_21_q), .b(notgate_22_q), .Q(andgate_71_q));
  Andgate andgate_72 (.a(notgate_19_q), .b(notgate_21_q), .Q(andgate_72_q));
  Andgate andgate_73 (.a(D), .b(notgate_23_q), .Q(andgate_73_q));
  Andgate andgate_74 (.a(A), .b(notgate_20_q), .Q(andgate_74_q));
  Andgate andgate_75 (.a(notgate_21_q), .b(notgate_22_q), .Q(andgate_75_q));
  Andgate andgate_76 (.a(notgate_25_q), .b(notgate_26_q), .Q(andgate_76_q));
  Andgate andgate_77 (.a(notgate_27_q), .b(D), .Q(andgate_77_q));
  Andgate andgate_78 (.a(notgate_25_q), .b(notgate_26_q), .Q(andgate_78_q));
  Andgate andgate_79 (.a(D), .b(E), .Q(andgate_79_q));
  Andgate andgate_80 (.a(notgate_25_q), .b(B), .Q(andgate_80_q));
  Andgate andgate_81 (.a(C), .b(D), .Q(andgate_81_q));
  Andgate andgate_82 (.a(notgate_25_q), .b(B), .Q(andgate_82_q));
  Andgate andgate_83 (.a(notgate_27_q), .b(D), .Q(andgate_83_q));
  Andgate andgate_84 (.a(notgate_25_q), .b(notgate_26_q), .Q(andgate_84_q));
  Andgate andgate_85 (.a(C), .b(notgate_29_q), .Q(andgate_85_q));
  Andgate andgate_86 (.a(notgate_25_q), .b(notgate_26_q), .Q(andgate_86_q));
  Andgate andgate_87 (.a(notgate_27_q), .b(notgate_28_q), .Q(andgate_87_q));
  Andgate andgate_88 (.a(notgate_25_q), .b(B), .Q(andgate_88_q));
  Andgate andgate_89 (.a(notgate_27_q), .b(D), .Q(andgate_89_q));
  Andgate andgate_90 (.a(notgate_25_q), .b(B), .Q(andgate_90_q));
  Andgate andgate_91 (.a(notgate_27_q), .b(notgate_28_q), .Q(andgate_91_q));
  Andgate andgate_92 (.a(notgate_25_q), .b(B), .Q(andgate_92_q));
  Andgate andgate_93 (.a(C), .b(notgate_28_q), .Q(andgate_93_q));
  Andgate andgate_94 (.a(notgate_31_q), .b(B), .Q(andgate_94_q));
  Andgate andgate_95 (.a(E), .b(F), .Q(andgate_95_q));
  Andgate andgate_96 (.a(notgate_31_q), .b(B), .Q(andgate_96_q));
  Andgate andgate_97 (.a(notgate_33_q), .b(notgate_35_q), .Q(andgate_97_q));
  Andgate andgate_98 (.a(notgate_31_q), .b(C), .Q(andgate_98_q));
  Andgate andgate_99 (.a(D), .b(notgate_36_q), .Q(andgate_99_q));
  Andgate andgate_100 (.a(notgate_31_q), .b(notgate_32_q), .Q(andgate_100_q));
  Andgate andgate_101 (.a(notgate_33_q), .b(E), .Q(andgate_101_q));
  Andgate andgate_102 (.a(notgate_31_q), .b(notgate_32_q), .Q(andgate_102_q));
  Andgate andgate_103 (.a(D), .b(notgate_35_q), .Q(andgate_103_q));
  Andgate andgate_104 (.a(notgate_31_q), .b(notgate_32_q), .Q(andgate_104_q));
  Andgate andgate_105 (.a(C), .b(notgate_35_q), .Q(andgate_105_q));
  Andgate andgate_106 (.a(notgate_32_q), .b(notgate_33_q), .Q(andgate_106_q));
  Andgate andgate_107 (.a(notgate_34_q), .b(notgate_35_q), .Q(andgate_107_q));
  Andgate andgate_108 (.a(notgate_31_q), .b(B), .Q(andgate_108_q));
  Andgate andgate_109 (.a(C), .b(notgate_34_q), .Q(andgate_109_q));
  Andgate andgate_110 (.a(notgate_31_q), .b(C), .Q(andgate_110_q));
  Andgate andgate_111 (.a(notgate_34_q), .b(E), .Q(andgate_111_q));
  Andgate andgate_112 (.a(notgate_37_q), .b(B), .Q(andgate_112_q));
  Andgate andgate_113 (.a(notgate_41_q), .b(F), .Q(andgate_113_q));
  Andgate andgate_114 (.a(notgate_37_q), .b(notgate_38_q), .Q(andgate_114_q));
  Andgate andgate_115 (.a(notgate_39_q), .b(notgate_41_q), .Q(andgate_115_q));
  Andgate andgate_116 (.a(notgate_37_q), .b(C), .Q(andgate_116_q));
  Andgate andgate_117 (.a(notgate_40_q), .b(notgate_42_q), .Q(andgate_117_q));
  Andgate andgate_118 (.a(notgate_37_q), .b(B), .Q(andgate_118_q));
  Andgate andgate_119 (.a(notgate_39_q), .b(D), .Q(andgate_119_q));
  Andgate andgate_120 (.a(notgate_37_q), .b(notgate_38_q), .Q(andgate_120_q));
  Andgate andgate_121 (.a(E), .b(F), .Q(andgate_121_q));
  Andgate andgate_122 (.a(notgate_37_q), .b(notgate_39_q), .Q(andgate_122_q));
  Andgate andgate_123 (.a(notgate_40_q), .b(E), .Q(andgate_123_q));
  Andgate andgate_124 (.a(notgate_38_q), .b(notgate_39_q), .Q(andgate_124_q));
  Andgate andgate_125 (.a(notgate_40_q), .b(notgate_41_q), .Q(andgate_125_q));
  Andgate andgate_126 (.a(notgate_37_q), .b(C), .Q(andgate_126_q));
  Andgate andgate_127 (.a(D), .b(notgate_41_q), .Q(andgate_127_q));
  Andgate andgate_128 (.a(notgate_37_q), .b(C), .Q(andgate_128_q));
  Andgate andgate_129 (.a(E), .b(D), .Q(andgate_129_q));
  Andgate andgate_130 (.a(notgate_37_q), .b(C), .Q(andgate_130_q));
  Andgate andgate_131 (.a(D), .b(notgate_41_q), .Q(andgate_131_q));
  Andgate andgate_132 (.a(notgate_37_q), .b(B), .Q(andgate_132_q));
  Andgate andgate_133 (.a(notgate_39_q), .b(D), .Q(andgate_133_q));
  Andgate andgate_134 (.a(notgate_37_q), .b(notgate_38_q), .Q(andgate_134_q));
  Andgate andgate_135 (.a(notgate_39_q), .b(D), .Q(andgate_135_q));
  Andgate andgate_136 (.a(notgate_37_q), .b(notgate_38_q), .Q(andgate_136_q));
  Andgate andgate_137 (.a(C), .b(D), .Q(andgate_137_q));
  Andgate andgate_138 (.a(notgate_37_q), .b(B), .Q(andgate_138_q));
  Andgate andgate_139 (.a(C), .b(notgate_40_q), .Q(andgate_139_q));
  Andgate andgate_140 (.a(notgate_37_q), .b(B), .Q(andgate_140_q));
  Andgate andgate_141 (.a(notgate_39_q), .b(D), .Q(andgate_141_q));
  Andgate andgate_142 (.a(notgate_37_q), .b(B), .Q(andgate_142_q));
  Andgate andgate_143 (.a(notgate_39_q), .b(notgate_40_q), .Q(andgate_143_q));
  Andgate andgate_144 (.a(notgate_37_q), .b(notgate_38_q), .Q(andgate_144_q));
  Andgate andgate_145 (.a(C), .b(D), .Q(andgate_145_q));
  Andgate andgate_146 (.a(andgate_1_q), .b(E), .Q(andgate_146_q));
  Andgate andgate_147 (.a(andgate_2_q), .b(notgate_6_q), .Q(andgate_147_q));
  Andgate andgate_148 (.a(andgate_3_q), .b(E), .Q(andgate_148_q));
  Andgate andgate_149 (.a(andgate_4_q), .b(notgate_4_q), .Q(andgate_149_q));
  Andgate andgate_150 (.a(andgate_5_q), .b(E), .Q(andgate_150_q));
  Andgate andgate_151 (.a(andgate_7_q), .b(F), .Q(andgate_151_q));
  Andgate andgate_152 (.a(andgate_9_q), .b(E), .Q(andgate_152_q));
  Andgate andgate_153 (.a(andgate_11_q), .b(notgate_5_q), .Q(andgate_153_q));
  Andgate andgate_154 (.a(andgate_12_q), .b(notgate_6_q), .Q(andgate_154_q));
  Andgate andgate_155 (.a(andgate_13_q), .b(notgate_6_q), .Q(andgate_155_q));
  Andgate andgate_156 (.a(andgate_15_q), .b(notgate_6_q), .Q(andgate_156_q));
  Andgate andgate_157 (.a(andgate_16_q), .b(A), .Q(andgate_157_q));
  Andgate andgate_158 (.a(andgate_17_q), .b(notgate_5_q), .Q(andgate_158_q));
  Andgate andgate_159 (.a(andgate_19_q), .b(notgate_5_q), .Q(andgate_159_q));
  Andgate andgate_160 (.a(andgate_20_q), .b(notgate_6_q), .Q(andgate_160_q));
  Andgate andgate_161 (.a(andgate_21_q), .b(notgate_5_q), .Q(andgate_161_q));
  Andgate andgate_162 (.a(andgate_22_q), .b(F), .Q(andgate_162_q));
  Andgate andgate_163 (.a(andgate_23_q), .b(andgate_24_q), .Q(andgate_163_q));
  Andgate andgate_164 (.a(andgate_25_q), .b(andgate_26_q), .Q(andgate_164_q));
  Andgate andgate_165 (.a(andgate_27_q), .b(andgate_28_q), .Q(andgate_165_q));
  Andgate andgate_166 (.a(andgate_29_q), .b(andgate_30_q), .Q(andgate_166_q));
  Andgate andgate_167 (.a(andgate_31_q), .b(notgate_12_q), .Q(andgate_167_q));
  Andgate andgate_168 (.a(andgate_33_q), .b(F), .Q(andgate_168_q));
  Andgate andgate_169 (.a(andgate_34_q), .b(notgate_10_q), .Q(andgate_169_q));
  Andgate andgate_170 (.a(andgate_35_q), .b(notgate_12_q), .Q(andgate_170_q));
  Andgate andgate_171 (.a(andgate_37_q), .b(F), .Q(andgate_171_q));
  Andgate andgate_172 (.a(andgate_39_q), .b(notgate_11_q), .Q(andgate_172_q));
  Andgate andgate_173 (.a(andgate_40_q), .b(F), .Q(andgate_173_q));
  Andgate andgate_174 (.a(andgate_41_q), .b(andgate_42_q), .Q(andgate_174_q));
  Andgate andgate_175 (.a(andgate_43_q), .b(andgate_44_q), .Q(andgate_175_q));
  Andgate andgate_176 (.a(andgate_45_q), .b(andgate_46_q), .Q(andgate_176_q));
  Andgate andgate_177 (.a(andgate_47_q), .b(andgate_48_q), .Q(andgate_177_q));
  Andgate andgate_178 (.a(andgate_49_q), .b(F), .Q(andgate_178_q));
  Andgate andgate_179 (.a(andgate_51_q), .b(F), .Q(andgate_179_q));
  Andgate andgate_180 (.a(andgate_53_q), .b(notgate_18_q), .Q(andgate_180_q));
  Andgate andgate_181 (.a(andgate_55_q), .b(notgate_16_q), .Q(andgate_181_q));
  Andgate andgate_182 (.a(andgate_57_q), .b(notgate_16_q), .Q(andgate_182_q));
  Andgate andgate_183 (.a(andgate_58_q), .b(notgate_13_q), .Q(andgate_183_q));
  Andgate andgate_184 (.a(andgate_59_q), .b(notgate_22_q), .Q(andgate_184_q));
  Andgate andgate_185 (.a(andgate_60_q), .b(andgate_61_q), .Q(andgate_185_q));
  Andgate andgate_186 (.a(andgate_62_q), .b(andgate_63_q), .Q(andgate_186_q));
  Andgate andgate_187 (.a(andgate_64_q), .b(andgate_65_q), .Q(andgate_187_q));
  Andgate andgate_188 (.a(andgate_66_q), .b(andgate_67_q), .Q(andgate_188_q));
  Andgate andgate_189 (.a(andgate_68_q), .b(andgate_69_q), .Q(andgate_189_q));
  Andgate andgate_190 (.a(andgate_70_q), .b(notgate_24_q), .Q(andgate_190_q));
  Andgate andgate_191 (.a(andgate_72_q), .b(notgate_24_q), .Q(andgate_191_q));
  Andgate andgate_192 (.a(andgate_73_q), .b(notgate_20_q), .Q(andgate_192_q));
  Andgate andgate_193 (.a(andgate_74_q), .b(notgate_23_q), .Q(andgate_193_q));
  Andgate andgate_194 (.a(andgate_75_q), .b(notgate_24_q), .Q(andgate_194_q));
  Andgate andgate_195 (.a(andgate_76_q), .b(E), .Q(andgate_195_q));
  Andgate andgate_196 (.a(andgate_78_q), .b(notgate_30_q), .Q(andgate_196_q));
  Andgate andgate_197 (.a(andgate_80_q), .b(notgate_30_q), .Q(andgate_197_q));
  Andgate andgate_198 (.a(andgate_82_q), .b(notgate_29_q), .Q(andgate_198_q));
  Andgate andgate_199 (.a(andgate_84_q), .b(F), .Q(andgate_199_q));
  Andgate andgate_200 (.a(andgate_86_q), .b(notgate_30_q), .Q(andgate_200_q));
  Andgate andgate_201 (.a(andgate_88_q), .b(E), .Q(andgate_201_q));
  Andgate andgate_202 (.a(andgate_89_q), .b(F), .Q(andgate_202_q));
  Andgate andgate_203 (.a(andgate_90_q), .b(notgate_29_q), .Q(andgate_203_q));
  Andgate andgate_204 (.a(andgate_91_q), .b(notgate_30_q), .Q(andgate_204_q));
  Andgate andgate_205 (.a(andgate_92_q), .b(E), .Q(andgate_205_q));
  Andgate andgate_206 (.a(andgate_93_q), .b(F), .Q(andgate_206_q));
  Andgate andgate_207 (.a(andgate_94_q), .b(andgate_95_q), .Q(andgate_207_q));
  Andgate andgate_208 (.a(andgate_96_q), .b(andgate_97_q), .Q(andgate_208_q));
  Andgate andgate_209 (.a(andgate_98_q), .b(andgate_99_q), .Q(andgate_209_q));
  Andgate andgate_210 (.a(andgate_100_q), .b(andgate_101_q), .Q(andgate_210_q));
  Andgate andgate_211 (.a(andgate_102_q), .b(F), .Q(andgate_211_q));
  Andgate andgate_212 (.a(andgate_104_q), .b(F), .Q(andgate_212_q));
  Andgate andgate_213 (.a(andgate_106_q), .b(notgate_36_q), .Q(andgate_213_q));
  Andgate andgate_214 (.a(andgate_107_q), .b(notgate_31_q), .Q(andgate_214_q));
  Andgate andgate_215 (.a(andgate_108_q), .b(notgate_36_q), .Q(andgate_215_q));
  Andgate andgate_216 (.a(andgate_110_q), .b(notgate_36_q), .Q(andgate_216_q));
  Andgate andgate_217 (.a(andgate_112_q), .b(andgate_113_q), .Q(andgate_217_q));
  Andgate andgate_218 (.a(andgate_114_q), .b(andgate_115_q), .Q(andgate_218_q));
  Andgate andgate_219 (.a(andgate_116_q), .b(andgate_117_q), .Q(andgate_219_q));
  Andgate andgate_220 (.a(andgate_118_q), .b(E), .Q(andgate_220_q));
  Andgate andgate_221 (.a(andgate_119_q), .b(notgate_42_q), .Q(andgate_221_q));
  Andgate andgate_222 (.a(andgate_120_q), .b(andgate_121_q), .Q(andgate_222_q));
  Andgate andgate_223 (.a(andgate_122_q), .b(F), .Q(andgate_223_q));
  Andgate andgate_224 (.a(andgate_124_q), .b(notgate_42_q), .Q(andgate_224_q));
  Andgate andgate_225 (.a(andgate_126_q), .b(notgate_42_q), .Q(andgate_225_q));
  Andgate andgate_226 (.a(andgate_128_q), .b(F), .Q(andgate_226_q));
  Andgate andgate_227 (.a(andgate_130_q), .b(notgate_42_q), .Q(andgate_227_q));
  Andgate andgate_228 (.a(andgate_132_q), .b(E), .Q(andgate_228_q));
  Andgate andgate_229 (.a(andgate_133_q), .b(notgate_42_q), .Q(andgate_229_q));
  Andgate andgate_230 (.a(andgate_134_q), .b(E), .Q(andgate_230_q));
  Andgate andgate_231 (.a(andgate_135_q), .b(notgate_42_q), .Q(andgate_231_q));
  Andgate andgate_232 (.a(andgate_136_q), .b(notgate_41_q), .Q(andgate_232_q));
  Andgate andgate_233 (.a(andgate_137_q), .b(F), .Q(andgate_233_q));
  Andgate andgate_234 (.a(andgate_138_q), .b(E), .Q(andgate_234_q));
  Andgate andgate_235 (.a(andgate_139_q), .b(F), .Q(andgate_235_q));
  Andgate andgate_236 (.a(andgate_140_q), .b(notgate_41_q), .Q(andgate_236_q));
  Andgate andgate_237 (.a(andgate_141_q), .b(notgate_42_q), .Q(andgate_237_q));
  Andgate andgate_238 (.a(andgate_142_q), .b(E), .Q(andgate_238_q));
  Andgate andgate_239 (.a(andgate_143_q), .b(notgate_42_q), .Q(andgate_239_q));
  Andgate andgate_240 (.a(andgate_144_q), .b(E), .Q(andgate_240_q));
  Andgate andgate_241 (.a(andgate_145_q), .b(notgate_42_q), .Q(andgate_241_q));
  Andgate andgate_242 (.a(andgate_146_q), .b(andgate_147_q), .Q(andgate_242_q));
  Andgate andgate_243 (.a(andgate_150_q), .b(andgate_6_q), .Q(andgate_243_q));
  Andgate andgate_244 (.a(andgate_151_q), .b(andgate_8_q), .Q(andgate_244_q));
  Andgate andgate_245 (.a(andgate_152_q), .b(andgate_10_q), .Q(andgate_245_q));
  Andgate andgate_246 (.a(andgate_153_q), .b(andgate_154_q), .Q(andgate_246_q));
  Andgate andgate_247 (.a(andgate_155_q), .b(andgate_14_q), .Q(andgate_247_q));
  Andgate andgate_248 (.a(andgate_156_q), .b(andgate_157_q), .Q(andgate_248_q));
  Andgate andgate_249 (.a(andgate_158_q), .b(andgate_18_q), .Q(andgate_249_q));
  Andgate andgate_250 (.a(andgate_159_q), .b(andgate_160_q), .Q(andgate_250_q));
  Andgate andgate_251 (.a(andgate_161_q), .b(andgate_162_q), .Q(andgate_251_q));
  Andgate andgate_252 (.a(andgate_167_q), .b(andgate_32_q), .Q(andgate_252_q));
  Andgate andgate_253 (.a(andgate_168_q), .b(andgate_169_q), .Q(andgate_253_q));
  Andgate andgate_254 (.a(andgate_170_q), .b(andgate_36_q), .Q(andgate_254_q));
  Andgate andgate_255 (.a(andgate_171_q), .b(andgate_38_q), .Q(andgate_255_q));
  Andgate andgate_256 (.a(andgate_172_q), .b(andgate_173_q), .Q(andgate_256_q));
  Orgate orgate_1 (.a(andgate_174_q), .b(andgate_175_q), .Q(orgate_1_q));
  Orgate orgate_2 (.a(andgate_176_q), .b(andgate_177_q), .Q(orgate_2_q));
  Andgate andgate_257 (.a(andgate_178_q), .b(andgate_50_q), .Q(andgate_257_q));
  Andgate andgate_258 (.a(andgate_179_q), .b(andgate_52_q), .Q(andgate_258_q));
  Andgate andgate_259 (.a(andgate_180_q), .b(andgate_54_q), .Q(andgate_259_q));
  Andgate andgate_260 (.a(andgate_181_q), .b(andgate_56_q), .Q(andgate_260_q));
  Andgate andgate_261 (.a(andgate_182_q), .b(andgate_183_q), .Q(andgate_261_q));
  Orgate orgate_3 (.a(andgate_184_q), .b(andgate_185_q), .Q(orgate_3_q));
  Orgate orgate_4 (.a(andgate_186_q), .b(andgate_187_q), .Q(orgate_4_q));
  Orgate orgate_5 (.a(andgate_188_q), .b(andgate_189_q), .Q(orgate_5_q));
  Andgate andgate_262 (.a(andgate_190_q), .b(andgate_71_q), .Q(andgate_262_q));
  Andgate andgate_263 (.a(andgate_191_q), .b(andgate_192_q), .Q(andgate_263_q));
  Andgate andgate_264 (.a(andgate_193_q), .b(andgate_194_q), .Q(andgate_264_q));
  Andgate andgate_265 (.a(andgate_195_q), .b(andgate_77_q), .Q(andgate_265_q));
  Andgate andgate_266 (.a(andgate_196_q), .b(andgate_79_q), .Q(andgate_266_q));
  Andgate andgate_267 (.a(andgate_197_q), .b(andgate_81_q), .Q(andgate_267_q));
  Andgate andgate_268 (.a(andgate_198_q), .b(andgate_83_q), .Q(andgate_268_q));
  Andgate andgate_269 (.a(andgate_199_q), .b(andgate_85_q), .Q(andgate_269_q));
  Andgate andgate_270 (.a(andgate_200_q), .b(andgate_87_q), .Q(andgate_270_q));
  Andgate andgate_271 (.a(andgate_201_q), .b(andgate_202_q), .Q(andgate_271_q));
  Andgate andgate_272 (.a(andgate_203_q), .b(andgate_204_q), .Q(andgate_272_q));
  Andgate andgate_273 (.a(andgate_205_q), .b(andgate_206_q), .Q(andgate_273_q));
  Orgate orgate_6 (.a(andgate_207_q), .b(andgate_208_q), .Q(orgate_6_q));
  Orgate orgate_7 (.a(andgate_209_q), .b(andgate_210_q), .Q(orgate_7_q));
  Andgate andgate_274 (.a(andgate_211_q), .b(andgate_103_q), .Q(andgate_274_q));
  Andgate andgate_275 (.a(andgate_212_q), .b(andgate_105_q), .Q(andgate_275_q));
  Andgate andgate_276 (.a(andgate_213_q), .b(andgate_214_q), .Q(andgate_276_q));
  Andgate andgate_277 (.a(andgate_215_q), .b(andgate_109_q), .Q(andgate_277_q));
  Andgate andgate_278 (.a(andgate_216_q), .b(andgate_111_q), .Q(andgate_278_q));
  Orgate orgate_8 (.a(andgate_217_q), .b(andgate_218_q), .Q(orgate_8_q));
  Orgate orgate_9 (.a(andgate_219_q), .b(andgate_279_q), .Q(orgate_9_q));
  Andgate andgate_279 (.a(andgate_220_q), .b(andgate_221_q), .Q(andgate_279_q));
  Andgate andgate_280 (.a(andgate_223_q), .b(andgate_123_q), .Q(andgate_280_q));
  Andgate andgate_281 (.a(andgate_224_q), .b(andgate_125_q), .Q(andgate_281_q));
  Andgate andgate_282 (.a(andgate_225_q), .b(andgate_127_q), .Q(andgate_282_q));
  Andgate andgate_283 (.a(andgate_226_q), .b(andgate_129_q), .Q(andgate_283_q));
  Andgate andgate_284 (.a(andgate_227_q), .b(andgate_131_q), .Q(andgate_284_q));
  Andgate andgate_285 (.a(andgate_228_q), .b(andgate_229_q), .Q(andgate_285_q));
  Andgate andgate_286 (.a(andgate_230_q), .b(andgate_231_q), .Q(andgate_286_q));
  Andgate andgate_287 (.a(andgate_232_q), .b(andgate_233_q), .Q(andgate_287_q));
  Andgate andgate_288 (.a(andgate_234_q), .b(andgate_235_q), .Q(andgate_288_q));
  Andgate andgate_289 (.a(andgate_236_q), .b(andgate_237_q), .Q(andgate_289_q));
  Andgate andgate_290 (.a(andgate_238_q), .b(andgate_239_q), .Q(andgate_290_q));
  Andgate andgate_291 (.a(andgate_240_q), .b(andgate_241_q), .Q(andgate_291_q));
  Orgate orgate_10 (.a(andgate_148_q), .b(andgate_149_q), .Q(orgate_10_q));
  Orgate orgate_11 (.a(andgate_243_q), .b(andgate_244_q), .Q(orgate_11_q));
  Orgate orgate_12 (.a(andgate_245_q), .b(andgate_246_q), .Q(orgate_12_q));
  Orgate orgate_13 (.a(andgate_248_q), .b(andgate_249_q), .Q(orgate_13_q));
  Orgate orgate_14 (.a(andgate_250_q), .b(andgate_251_q), .Q(orgate_14_q));
  Orgate orgate_15 (.a(andgate_163_q), .b(andgate_164_q), .Q(orgate_15_q));
  Orgate orgate_16 (.a(andgate_165_q), .b(andgate_166_q), .Q(orgate_16_q));
  Orgate orgate_17 (.a(andgate_252_q), .b(andgate_253_q), .Q(orgate_17_q));
  Orgate orgate_18 (.a(orgate_19_q), .b(andgate_256_q), .Q(orgate_18_q));
  Orgate orgate_19 (.a(andgate_254_q), .b(andgate_255_q), .Q(orgate_19_q));
  Orgate orgate_20 (.a(orgate_1_q), .b(orgate_2_q), .Q(orgate_20_q));
  Orgate orgate_21 (.a(andgate_257_q), .b(andgate_258_q), .Q(orgate_21_q));
  Orgate orgate_22 (.a(andgate_259_q), .b(andgate_260_q), .Q(orgate_22_q));
  Orgate orgate_23 (.a(orgate_3_q), .b(orgate_4_q), .Q(orgate_23_q));
  Orgate orgate_24 (.a(andgate_262_q), .b(andgate_263_q), .Q(orgate_24_q));
  Orgate orgate_25 (.a(andgate_266_q), .b(andgate_267_q), .Q(orgate_25_q));
  Orgate orgate_26 (.a(andgate_268_q), .b(andgate_269_q), .Q(orgate_26_q));
  Orgate orgate_27 (.a(andgate_270_q), .b(andgate_271_q), .Q(orgate_27_q));
  Orgate orgate_28 (.a(andgate_272_q), .b(andgate_273_q), .Q(orgate_28_q));
  Orgate orgate_29 (.a(orgate_6_q), .b(orgate_7_q), .Q(orgate_29_q));
  Orgate orgate_30 (.a(andgate_274_q), .b(andgate_275_q), .Q(orgate_30_q));
  Orgate orgate_31 (.a(andgate_276_q), .b(andgate_277_q), .Q(orgate_31_q));
  Orgate orgate_32 (.a(orgate_8_q), .b(orgate_9_q), .Q(orgate_32_q));
  Orgate orgate_33 (.a(andgate_222_q), .b(andgate_280_q), .Q(orgate_33_q));
  Orgate orgate_34 (.a(andgate_282_q), .b(andgate_283_q), .Q(orgate_34_q));
  Orgate orgate_35 (.a(andgate_284_q), .b(andgate_285_q), .Q(orgate_35_q));
  Orgate orgate_36 (.a(andgate_286_q), .b(andgate_287_q), .Q(orgate_36_q));
  Orgate orgate_37 (.a(orgate_38_q), .b(orgate_39_q), .Q(orgate_37_q));
  Orgate orgate_38 (.a(andgate_288_q), .b(andgate_289_q), .Q(orgate_38_q));
  Orgate orgate_39 (.a(andgate_290_q), .b(andgate_291_q), .Q(orgate_39_q));
  Orgate orgate_40 (.a(orgate_15_q), .b(orgate_16_q), .Q(orgate_40_q));
  Orgate orgate_41 (.a(orgate_17_q), .b(orgate_18_q), .Q(orgate_41_q));
  Orgate orgate_42 (.a(orgate_21_q), .b(orgate_22_q), .Q(orgate_42_q));
  Orgate orgate_43 (.a(orgate_5_q), .b(orgate_24_q), .Q(orgate_43_q));
  Orgate orgate_44 (.a(orgate_25_q), .b(orgate_26_q), .Q(orgate_44_q));
  Orgate orgate_45 (.a(orgate_27_q), .b(orgate_28_q), .Q(orgate_45_q));
  Orgate orgate_46 (.a(orgate_31_q), .b(andgate_278_q), .Q(orgate_46_q));
  Orgate orgate_47 (.a(orgate_32_q), .b(orgate_33_q), .Q(orgate_47_q));
  Orgate orgate_48 (.a(andgate_281_q), .b(orgate_34_q), .Q(orgate_48_q));
  Orgate orgate_49 (.a(orgate_35_q), .b(orgate_50_q), .Q(orgate_49_q));
  Orgate orgate_50 (.a(orgate_36_q), .b(orgate_37_q), .Q(orgate_50_q));
  Orgate orgate_51 (.a(orgate_10_q), .b(orgate_11_q), .Q(orgate_51_q));
  Orgate orgate_52 (.a(orgate_12_q), .b(andgate_247_q), .Q(orgate_52_q));
  Orgate orgate_53 (.a(orgate_13_q), .b(orgate_14_q), .Q(orgate_53_q));
  Orgate orgate_54 (.a(orgate_40_q), .b(orgate_41_q), .Q(Q2));
  Orgate orgate_55 (.a(orgate_20_q), .b(orgate_42_q), .Q(orgate_55_q));
  Orgate orgate_56 (.a(orgate_23_q), .b(orgate_43_q), .Q(orgate_56_q));
  Orgate orgate_57 (.a(orgate_44_q), .b(orgate_45_q), .Q(orgate_57_q));
  Orgate orgate_58 (.a(orgate_30_q), .b(orgate_46_q), .Q(orgate_58_q));
  Orgate orgate_59 (.a(orgate_48_q), .b(orgate_49_q), .Q(orgate_59_q));
  Orgate orgate_60 (.a(orgate_51_q), .b(orgate_52_q), .Q(orgate_60_q));
  Orgate orgate_61 (.a(orgate_55_q), .b(andgate_261_q), .Q(Q3));
  Orgate orgate_62 (.a(orgate_56_q), .b(andgate_264_q), .Q(Q4));
  Orgate orgate_63 (.a(andgate_265_q), .b(orgate_57_q), .Q(Q5));
  Orgate orgate_64 (.a(orgate_29_q), .b(orgate_58_q), .Q(Q6));
  Orgate orgate_65 (.a(orgate_47_q), .b(orgate_59_q), .Q(Q7));
  Orgate orgate_66 (.a(orgate_60_q), .b(orgate_53_q), .Q(orgate_66_q));
  Orgate orgate_67 (.a(andgate_242_q), .b(orgate_66_q), .Q(Q1));
endmodule
